// Digital circuit 7405A.dig as structural Verilog
// hex inverter, open-collector output
module _7405A (
  input  _1A,
  input  _2A,
  input  _3A,
  input  _4A,
  input  _5A,
  input  _6A,
  input  VCC,
  input  GND,
  output _1Y,
  output _2Y,
  output _3Y,
  output _4Y,
  output _5Y,
  output _6Y
);

  not not_1 (_1Y, _1A);
  not not_2 (_2Y, _2A);
  not not_3 (_3Y, _3A);
  PowerSupply powersupply_1 (.VDD(VCC), .GND(GND));
  not not_4 (_4Y, _4A);
  not not_5 (_5Y, _5A);
  not not_6 (_6Y, _6A);

  // Notes on the sheet:
  //   _1A: pin 1
  //   _1Y: pin 2
  //   _2A: pin 3
  //   _2Y: pin 4
  //   _3A: pin 5
  //   _3Y: pin 6
  //   _4A: pin 9
  //   _4Y: pin 8
  //   _5A: pin 11
  //   _5Y: pin 10
  //   _6A: pin 13
  //   _6Y: pin 12
  //   VCC: pin 14, default 1
  //   GND: pin 7
endmodule
