// Digital circuit ALU.dig as structural Verilog
module ALU (
  input  A0,
  input  A1,
  input  A2,
  input  A3,
  input  A4,
  input  A5,
  input  A6,
  input  A7,
  input  B0,
  input  B1,
  input  B2,
  input  B3,
  input  B4,
  input  B5,
  input  B6,
  input  B7,
  input  S0,
  input  S1,
  input  S2,
  input  S3,
  input  M,
  input  CIN,
  input  F,
  output C0,
  output C1,
  output C2,
  output C3,
  output C4,
  output C5,
  output C6,
  output C7,
  output Z,
  output EQ,
  output COUT
);

  wire AdderLower_pin9, AdderLower_pin10, AdderLower_pin11, AdderUpper_pin7, AdderUpper_pin9,
       AdderUpper_pin10, AdderUpper_pin11, not_1_out, not_2_out, not_3_out, not_4_out, not_5_out, not_6_out,
       not_7_out, not_8_out, not_9_out, not_10_out, not_11_out, not_12_out, not_13_out, not_14_out,
       not_15_out, not_16_out, undriven, undriven_2, undriven_4, undriven_5;
  wire [2:0] and_11_out;
  wire [7:0] and_8_out, or_8_out, xor_8_out;
  wire [8:0] undriven_3;

  xor xor_1 (xor_8_out[7], B7, A7);
  xor xor_2 (xor_8_out[6], B6, A6);
  xor xor_3 (xor_8_out[5], B5, A5);
  xor xor_4 (xor_8_out[4], B4, A4);
  xor xor_5 (xor_8_out[3], B3, A3);
  xor xor_6 (xor_8_out[2], B2, A2);
  xor xor_7 (xor_8_out[1], B1, A1);
  xor xor_8 (xor_8_out[0], B0, A0);
  or or_1 (or_8_out[7], B7, A7);
  or or_2 (or_8_out[6], B6, A6);
  or or_3 (or_8_out[5], B5, A5);
  or or_4 (or_8_out[4], B4, A4);
  or or_5 (or_8_out[3], B3, A3);
  or or_6 (or_8_out[2], B2, A2);
  or or_7 (or_8_out[1], B1, A1);
  or or_8 (or_8_out[0], B0, A0);
  and and_1 (and_8_out[7], B7, A7);
  and and_2 (and_8_out[6], B6, A6);
  and and_3 (and_8_out[5], B5, A5);
  and and_4 (and_8_out[4], B4, A4);
  and and_5 (and_8_out[3], B3, A3);
  and and_6 (and_8_out[2], B2, A2);
  and and_7 (and_8_out[1], B1, A1);
  and and_8 (and_8_out[0], B0, A0);
  and and_9 (and_11_out[2], S2, F);
  and and_10 (and_11_out[1], S1, F);
  and and_11 (and_11_out[0], S0, F);
  not not_1 (not_1_out, A7);
  not not_2 (not_2_out, A6);
  not not_3 (not_3_out, A5);
  not not_4 (not_4_out, A4);
  not not_5 (not_5_out, A3);
  not not_6 (not_6_out, A2);
  not not_7 (not_7_out, A1);
  not not_8 (not_8_out, A0);
  not not_9 (not_9_out, B7);
  not not_10 (not_10_out, B6);
  not not_11 (not_11_out, B5);
  not not_12 (not_12_out, B4);
  not not_13 (not_13_out, B3);
  not not_14 (not_14_out, B2);
  not not_15 (not_15_out, B1);
  not not_16 (not_16_out, B0);
  _74181 AdderUpper (
    .pin1(not_12_out), .pin2(not_4_out), .pin3(S3), .pin4(S2), .pin5(S1), .pin6(S0), .pin7(AdderUpper_pin7),
    .pin8(M), .pin9(AdderUpper_pin9), .pin10(AdderUpper_pin10), .pin11(AdderUpper_pin11), .pin12(1'b0));  // open: pin13, pin14, pin15, pin16, pin17, pin18, pin19, pin20, pin21, pin22, pin23, pin24
  _74181 AdderLower (
    .pin1(not_16_out), .pin2(not_8_out), .pin3(S3), .pin4(S2), .pin5(S1), .pin6(S0), .pin7(CIN), .pin8(M),
    .pin9(AdderLower_pin9), .pin10(AdderLower_pin10), .pin11(AdderLower_pin11), .pin12(1'b0));  // open: pin13, pin14, pin15, pin16, pin17, pin18, pin19, pin20, pin21, pin22, pin23, pin24
  not not_17 (undriven_3[7], undriven_4);
  not not_18 (undriven_3[6], AdderUpper_pin11);
  not not_19 (undriven_3[5], AdderUpper_pin10);
  not not_20 (undriven_3[4], AdderUpper_pin9);
  not not_21 (undriven_3[3], undriven_5);
  not not_22 (undriven_3[2], AdderLower_pin11);
  not not_23 (undriven_3[1], AdderLower_pin10);
  not not_24 (undriven_3[0], AdderLower_pin9);
  Multiplexer #(.Selector_Bits(3), .Bits(9)) multiplexer_1 (
    .sel(and_11_out), .in_0(undriven_3), .in_1({A0, 1'b0, A7, A6, A5, A4, A3, A2, A1}),
    .in_2({A7, A6, A5, A4, A3, A2, A1, A0, 1'b0}), .in_3({A0, CIN, A7, A6, A5, A4, A3, A2, A1}),
    .in_4({A7, A6, A5, A4, A3, A2, A1, A0, CIN}), .in_5({1'b0, and_8_out}), .in_6({1'b0, or_8_out}),
    .in_7({1'b0, xor_8_out}), .out({COUT, C7, C6, C5, C4, C3, C2, C1, C0}));
  nor nor_1 (Z, C7, C6, C5, C4, C3, C2, C1, C0);
  Seven_Seg_Hex seven_seg_hex_1 (.d({1'b0, and_11_out}), .dp(1'b0));
  and and_12 (EQ, undriven, undriven_2);

  // Notes on the sheet:
  //   LRL - Logical Rotate Left - 4
  //   LRR - Logical Rotate Right - 3
  //   LSL - Logical Shift Left - 2
  //   LSR - Logical Shift Right - 1
  //   XOR - True if bit not the same - 7
  //   OR - True if either bits true - 6
  //   AND - True if both bits true - 5
endmodule
