// Digital circuit BRANCH.dig as structural Verilog
module BRANCH (
  input  EQ,
  input  C,
  input  Z,
  input  NEG,
  input  CLK,
  input  EQ_CTRL,
  input  C_CTRL,
  input  Z_CTRL,
  input  NEG_CTRL
);

  wire _7404_1_pin2, _7404_1_pin4, _7404_1_pin6, _7404_1_pin8, _7432_1_pin1, _7432_1_pin2, _7432_1_pin3,
       _7432_1_pin5, _7432_1_pin6, _7432_1_pin10, _7432_1_pin12, _7432_1_pin13;

  _7404 _7404_1 (
    .pin1(EQ), .pin2(_7404_1_pin2), .pin3(C), .pin4(_7404_1_pin4), .pin5(Z), .pin6(_7404_1_pin6),
    .pin7(1'b0), .pin8(_7404_1_pin8), .pin9(NEG), .pin11(1'b0), .pin13(1'b0), .pin14(1'b1));  // open: pin10, pin12
  _7432 _7432_1 (
    .pin1(_7432_1_pin1), .pin2(_7432_1_pin2), .pin3(_7432_1_pin3), .pin4(_7432_1_pin3), .pin5(_7432_1_pin5),
    .pin6(_7432_1_pin6), .pin7(1'b0), .pin8(_7432_1_pin5), .pin9(CLK), .pin10(_7432_1_pin10),
    .pin11(_7432_1_pin10), .pin12(_7432_1_pin12), .pin13(_7432_1_pin13), .pin14(1'b1));
  _7408 _7408_1 (
    .pin1(EQ_CTRL), .pin2(_7404_1_pin2), .pin3(_7432_1_pin2), .pin4(C_CTRL), .pin5(_7404_1_pin4),
    .pin6(_7432_1_pin1), .pin7(1'b0), .pin8(_7432_1_pin12), .pin9(Z_CTRL), .pin10(_7404_1_pin6),
    .pin11(_7432_1_pin13), .pin12(NEG_CTRL), .pin13(_7404_1_pin8), .pin14(1'b1));
  LED led_1 (.in(_7432_1_pin6));
endmodule
