// Digital circuit CLK.dig as structural Verilog
module CLK (
  input  Clock,
  input  S2,
  input  S1,
  input  S0,
  input  HALT,
  input  RST,
  input  S3,
  output CLK,
  output LOAD,
  output ENABLE,
  output CC0,
  output CC1,
  output CC2,
  output CC3,
  output CC4,
  output CC5,
  output CC6,
  output CC7,
  output CC8,
  output CC9,
  output PUSH,
  output POP,
  output SWP,
  output CLR,
  output CLRIRQ,
  output CLRSUPIRQ,
  output SETIRQ,
  output [3:0] DISPLAY
);

  wire _74154_1_pin1, _74154_1_pin2, _74154_1_pin3, _74154_1_pin4, _74154_1_pin5, _74154_1_pin6,
       _74154_1_pin7, _74154_1_pin8, _74154_1_pin9, _74154_1_pin10, _744017_1_pin15, and_1_out, and_2_out,
       and_3_out, and_4_out, and_5_out, and_6_out, and_7_out, and_8_out, and_9_out, and_10_out, and_11_out,
       driver_24_out, driver_30_out, not_1_out, not_2_out, not_3_out, not_4_out, not_5_out, not_6_out,
       not_7_out, not_8_out, not_9_out, not_10_out, not_11_out, or_1_out, or_2_out, or_4_out, or_5_out,
       or_6_out, or_7_out, or_8_out, or_9_out, or_10_out, or_11_out, or_12_out, or_13_out, or_14_out,
       or_15_out, or_16_out, or_17_out, or_18_out, or_19_out, or_20_out, or_21_out, or_22_out, or_23_out,
       rs_ff_as_1_q;

  Switch switch_1 (.A(1'b1), .B(Clock));
  PullDown pulldown_1 (.out(HALT));
  PullDown pulldown_2 (.out(Clock));
  Register_SepOut4 register_sepout4_1 (
    .D3(S3), .D2(S2), .D1(S1), .D0(S0), .LOAD(CC0), .RST(RST), .EOUT(1'b0), .EIN(or_1_out), .M0(DISPLAY[0]),
    .M1(DISPLAY[1]), .M2(DISPLAY[2]), .M3(DISPLAY[3]));  // open: Q3, Q2, Q1, Q0
  _74154 _74154_1 (
    .pin1(_74154_1_pin1), .pin2(_74154_1_pin2), .pin3(_74154_1_pin3), .pin4(_74154_1_pin4),
    .pin5(_74154_1_pin5), .pin6(_74154_1_pin6), .pin7(_74154_1_pin7), .pin8(_74154_1_pin8),
    .pin9(_74154_1_pin9), .pin10(_74154_1_pin10), .pin12(1'b0), .pin18(1'b0), .pin19(1'b0),
    .pin20(DISPLAY[3]), .pin21(DISPLAY[2]), .pin22(DISPLAY[1]), .pin23(DISPLAY[0]), .pin24(1'b1));  // open: pin11, pin13, pin14, pin15, pin16, pin17
  or or_1 (or_1_out, _744017_1_pin15, CC0);
  not not_1 (not_1_out, HALT);
  not not_2 (not_2_out, _74154_1_pin3);
  not not_3 (not_3_out, _74154_1_pin6);
  not not_4 (not_4_out, _74154_1_pin7);
  not not_5 (not_5_out, _74154_1_pin8);
  not not_6 (not_6_out, _74154_1_pin9);
  not not_7 (not_7_out, _74154_1_pin10);
  not not_8 (not_8_out, _74154_1_pin1);
  not not_9 (not_9_out, _74154_1_pin2);
  not not_10 (not_10_out, _74154_1_pin4);
  not not_11 (not_11_out, _74154_1_pin5);
  and and_1 (and_1_out, not_3_out, rs_ff_as_1_q, CC5);
  and and_2 (and_2_out, not_4_out, rs_ff_as_1_q, CC3);
  and and_3 (and_3_out, not_5_out, rs_ff_as_1_q, CC8);
  and and_4 (and_4_out, not_6_out, rs_ff_as_1_q, CC6);
  and and_5 (and_5_out, not_7_out, rs_ff_as_1_q, CC3);
  and and_6 (and_6_out, Clock, not_1_out);
  _744017 _744017_1 (
    .pin1(CC5), .pin2(CC1), .pin3(CC0), .pin4(CC2), .pin5(CC6), .pin6(CC7), .pin7(CC3), .pin8(1'b0),
    .pin9(CC8), .pin10(CC4), .pin11(CC9), .pin13(1'b0), .pin14(and_6_out), .pin15(_744017_1_pin15),
    .pin16(1'b1));  // open: pin12
  and and_7 (and_7_out, not_8_out, rs_ff_as_1_q, CC2);
  and and_8 (and_8_out, not_9_out, rs_ff_as_1_q, CC4);
  and and_9 (and_9_out, not_2_out, rs_ff_as_1_q, CC8);
  and and_10 (and_10_out, not_10_out, rs_ff_as_1_q, CC8);
  and and_11 (and_11_out, not_11_out, rs_ff_as_1_q, CC5);
  or or_2 (or_2_out, and_7_out, and_8_out, and_5_out, and_9_out, and_10_out);
  or or_3 (_744017_1_pin15, or_2_out, CC9, or_4_out);
  or or_4 (or_4_out, and_11_out, and_1_out, and_4_out, and_3_out, and_2_out);
  PullDown pulldown_3 (.out(CC1));
  PullDown pulldown_4 (.out(CC2));
  PullDown pulldown_5 (.out(CC3));
  PullDown pulldown_6 (.out(CC4));
  PullDown pulldown_7 (.out(CC5));
  PullDown pulldown_8 (.out(CC6));
  PullDown pulldown_9 (.out(CC7));
  PullDown pulldown_10 (.out(CC8));
  PullDown pulldown_11 (.out(CC9));
  or or_5 (or_5_out, CC1, CC2);
  or or_6 (or_6_out, CC7, CC6, CC5);
  or or_7 (or_7_out, CC4, CC3);
  or or_8 (or_8_out, CC4, CC2);
  or or_9 (or_9_out, CC7, CC6, CC2, CC1);
  or or_10 (or_10_out, CC7, CC5);
  or or_11 (or_11_out, CC4, CC5, CC2);
  or or_12 (or_12_out, CC4, CC5, CC3);
  or or_13 (or_13_out, CC2, CC1);
  or or_14 (or_14_out, CC2, CC1);
  or or_15 (or_15_out, CC3, CC2);
  or or_16 (or_16_out, CC2, CC1);
  or or_17 (or_17_out, CC7, CC6, CC5);
  or or_18 (or_18_out, CC4, CC3);
  or or_19 (or_19_out, CC4, CC2);
  or or_20 (or_20_out, CC7, CC2, CC1, CC6);
  or or_21 (or_21_out, CC1, CC2);
  or or_22 (or_22_out, CC2, CC4);
  or or_23 (or_23_out, CC3, CC4);
  RS_FF_AS rs_ff_as_1 (.S(_744017_1_pin15), .R(RST), .Q(rs_ff_as_1_q), .nQ(CLR));
  assign CLK = not_8_out ? CC1 : 1'bz;  // Driver driver_1
  assign CLK = not_9_out ? CC3 : 1'bz;  // Driver driver_2
  assign LOAD = not_9_out ? CC2 : 1'bz;  // Driver driver_3
  assign ENABLE = not_9_out ? or_5_out : 1'bz;  // Driver driver_4
  assign CLK = not_2_out ? CC7 : 1'bz;  // Driver driver_5
  assign SWP = not_2_out ? or_6_out : 1'bz;  // Driver driver_6
  assign PUSH = not_2_out ? or_7_out : 1'bz;  // Driver driver_7
  assign LOAD = not_2_out ? or_8_out : 1'bz;  // Driver driver_8
  assign ENABLE = not_2_out ? or_9_out : 1'bz;  // Driver driver_9
  assign CLK = not_10_out ? or_10_out : 1'bz;  // Driver driver_10
  assign LOAD = not_10_out ? or_11_out : 1'bz;  // Driver driver_11
  assign ENABLE = not_10_out ? or_12_out : 1'bz;  // Driver driver_12
  assign POP = not_10_out ? or_13_out : 1'bz;  // Driver driver_13
  assign CLK = not_11_out ? CC4 : 1'bz;  // Driver driver_14
  assign PUSH = not_11_out ? CC3 : 1'bz;  // Driver driver_15
  assign LOAD = not_11_out ? CC2 : 1'bz;  // Driver driver_16
  assign ENABLE = not_11_out ? or_14_out : 1'bz;  // Driver driver_17
  assign CLK = not_3_out ? CC4 : 1'bz;  // Driver driver_18
  assign LOAD = not_3_out ? CC3 : 1'bz;  // Driver driver_19
  assign ENABLE = not_3_out ? or_15_out : 1'bz;  // Driver driver_20
  assign POP = not_3_out ? CC1 : 1'bz;  // Driver driver_21
  assign CLK = not_4_out ? CC2 : 1'bz;  // Driver driver_22
  assign ENABLE = not_4_out ? or_16_out : 1'bz;  // Driver driver_23
  assign driver_24_out = not_5_out ? CC7 : 1'bz;  // Driver driver_24
  assign CLK = not_5_out ? CC7 : 1'bz;  // Driver driver_25
  assign SWP = not_5_out ? or_17_out : 1'bz;  // Driver driver_26
  assign PUSH = not_5_out ? or_18_out : 1'bz;  // Driver driver_27
  assign LOAD = not_5_out ? or_19_out : 1'bz;  // Driver driver_28
  assign ENABLE = not_5_out ? or_20_out : 1'bz;  // Driver driver_29
  assign driver_30_out = not_6_out ? CC5 : 1'bz;  // Driver driver_30
  assign driver_24_out = not_6_out ? CC5 : 1'bz;  // Driver driver_31
  assign POP = not_6_out ? or_21_out : 1'bz;  // Driver driver_32
  assign CLK = not_6_out ? CC5 : 1'bz;  // Driver driver_33
  assign LOAD = not_6_out ? or_22_out : 1'bz;  // Driver driver_34
  assign ENABLE = not_6_out ? or_23_out : 1'bz;  // Driver driver_35
  assign SETIRQ = not_7_out ? CC2 : 1'bz;  // Driver driver_36
  assign CLK = not_7_out ? CC2 : 1'bz;  // Driver driver_37
  PullDown pulldown_12 (.out(POP));
  PullDown pulldown_13 (.out(SWP));
  PullDown pulldown_14 (.out(PUSH));
  PullDown pulldown_15 (.out(CLK));
  PullDown pulldown_16 (.out(LOAD));
  PullDown pulldown_17 (.out(ENABLE));
  PullDown pulldown_18 (.out(driver_24_out));
  PullDown pulldown_19 (.out(driver_30_out));
  PullDown pulldown_20 (.out(SETIRQ));
  or or_24 (CLRSUPIRQ, CLR, driver_30_out);
  or or_25 (CLRIRQ, CLR, driver_24_out);

  // Notes on the sheet:
  //   JSI - 7
  //   1. ENABLE
  //   2. ENABLE, LOAD
  //   3. PUSH
  //   4. PUSH, LOAD
  //   5. SWP
  //   6. SWP, ENABLE
  //   7. SWP, ENABLE, CLK, CLRIRQ
  //   RTI - 8
  //   1. POP
  //   2. POP, LOAD
  //   3. ENABLE
  //   4. ENABLE, LOAD
  //   5. CLK, CLRIRQ, CLRSUPIRQ
  //   RTN - 3
  //   1. POP
  //   2. POP, LOAD
  //   3. ENABLE
  //   4. ENABLE, LOAD
  //   5.  ENABLE, LOAD, CLK
  //   6. NULL
  //   7. CLK
  //   PUSH - 4
  //   1. ENABLE
  //   2. ENABLE, LOAD
  //   3. PUSH
  //   4. LOAD
  //   5. CLK
  //   POP - 5
  //   1. POP
  //   2. LOAD
  //   3. ENABLE
  //   4. ENABLE, LOAD
  //   5. CLK
  //   JMP - 6
  //   1. ENABLE
  //   2. ENABLE, CLK
  //   SI - 9
  //   0. SETIRQ, CLK
  //   JSR - 2
  //   1. ENABLE
  //   2. ENABLE, LOAD
  //   3. PUSH
  //   4. PUSH, LOAD
  //   5. SWP
  //   6. SWP, ENABLE
  //   7. SWP, ENABLE, CLK
  //   POP
  //   JMP
  //   JSI
  //   SI
  //   CLK
  //   STD
  //   JSR
  //   RTN
  //   PUSH
  //   CLK - 0
  //   1. CLK
  //   STD - 1
  //   1. ENABLE
  //   2. ENABLE, LOAD
  //   3. CLK
  //   CLK - 0
  //   STD - 1
  //   JBR - 2
  //   SWP
  //   LOAD
  //   ENABLE
  //   RTN - 3
  //   PUSH - 4
  //   POP - 5
  //   JMP - 6
  //   JSI - 7
  //   CLRSUPIRQ
  //   CLRIRQ
  //   SETIRQ
endmodule
