// Digital circuit CPU.dig as structural Verilog
module CPU (
);

  wire alu_1_c0, alu_1_c1, alu_1_c2, alu_1_c3, alu_1_c4, alu_1_c5, alu_1_c6, alu_1_c7, alu_1_cout, alu_1_eq,
       alu_1_z, decode_1_halt, decode_1_p0, decode_1_p1, decode_1_p2, decode_1_pc_ein, decode_1_pc_eout,
       decode_1_rega_ein, decode_1_rega_eout, decode_1_regb_ein, decode_1_regb_eout, decode_1_regc_ein,
       decode_1_regc_eout, decode_1_regf1_ein, decode_1_regf1_eout, decode_1_regf2_ein, decode_1_regf2_eout,
       decode_1_regs1_ein, decode_1_regs1_eout, decode_1_regs2_ein, decode_1_regs2_eout, decode_1_rst,
       decode_1_s0, decode_1_s1, decode_1_s2, decode_1_s3, decode_1_stk_eout, mmu_1_p3, mmu_1_p4, mmu_1_p5,
       mmu_1_p6, mmu_1_p7, mmu_1_p8, mmu_1_p9, mmu_1_p10, mmu_1_p11, mmu_1_p12, mmu_1_p13, mmu_1_p14,
       mmu_1_p15, mmu_1_p16, pulldown_25_out, pulldown_26_out, pulldown_27_out, pulldown_28_out,
       pulldown_29_out, pulldown_30_out, pulldown_31_out, pulldown_32_out, pulldown_33_out, pulldown_34_out,
       pulldown_35_out, pulldown_36_out, pulldown_37_out, pulldown_38_out, pulldown_39_out, pulldown_40_out,
       pulldown_41_out, pulldown_42_out, pulldown_43_out, pulldown_44_out, pulldown_45_out, pulldown_46_out,
       pulldown_47_out, pulldown_48_out, pulldown_49_out, pulldown_50_out, pulldown_51_out, pulldown_52_out,
       pulldown_53_out, pulldown_54_out, pulldown_55_out, pulldown_56_out, pulldown_57_out, pulldown_58_out,
       pulldown_59_out, pulldown_60_out, pulldown_61_out, pulldown_62_out, pulldown_63_out, pulldown_64_out,
       pulldown_65_out, pulldown_66_out, pulldown_67_out, pulldown_68_out, pulldown_69_out, pulldown_70_out,
       pulldown_71_out, pulldown_72_out, pulldown_73_out, pulldown_74_out, pulldown_75_out, pulldown_76_out,
       reg4_1_m0, reg4_1_m1, reg4_1_m2, reg4_1_m3, reg8_1_m0, reg8_1_m1, reg8_1_m2, reg8_1_m3, reg8_1_m4,
       reg8_1_m5, reg8_1_m6, reg8_1_m7, reg8_2_m0, reg8_2_m1, reg8_2_m2, reg8_2_m3, reg8_2_m4, reg8_2_m5,
       reg8_2_m6, reg8_2_m7, reg8_3_m0, reg8_3_m1, reg8_3_m2, reg8_3_m3, reg8_3_m4, reg8_3_m5, reg8_3_m6,
       reg8_3_m7, rom_1_p12, rom_1_p13, rom_1_p30, rom_1_p31, rom_1_p32, rom_1_p33, rom_1_p34, rom_1_p35,
       rom_1_p36, rom_1_p37, undriven, undriven_2, undriven_4, undriven_5, undriven_6, undriven_7,
       undriven_8, undriven_9, undriven_10, undriven_11, undriven_12, undriven_13, undriven_14, undriven_15,
       undriven_16, undriven_17, undriven_18, undriven_19, undriven_20;
  wire [3:0] pc_1_a0, pc_1_a4, pc_1_a8, pc_1_a12, pulldown_20_out, pulldown_24_out, rom_1_p1, rom_1_p8,
       rom_1_p17, rom_1_p21;
  wire [7:0] undriven_3;

  PC pc_1 (
    .D7(pulldown_20_out[3]), .D6(pulldown_20_out[2]), .D5(pulldown_20_out[1]), .D4(pulldown_20_out[0]),
    .D3(pulldown_24_out[3]), .D2(pulldown_24_out[2]), .D1(pulldown_24_out[1]), .D0(pulldown_24_out[0]),
    .A7(pc_1_a4[3]), .A6(pc_1_a4[2]), .A5(pc_1_a4[1]), .A4(pc_1_a4[0]), .A3(pc_1_a0[3]), .A2(pc_1_a0[2]),
    .A1(pc_1_a0[1]), .A0(pc_1_a0[0]), .A8(pc_1_a8[0]), .A9(pc_1_a8[1]), .A10(pc_1_a8[2]), .A11(pc_1_a8[3]),
    .A12(pc_1_a12[0]), .A13(pc_1_a12[1]), .A14(pc_1_a12[2]), .A15(pc_1_a12[3]));
  LED A14 (.in(pc_1_a12[2]));
  LED A15 (.in(pc_1_a12[3]));
  PullDown pulldown_1 (.out(pc_1_a12[2]));
  PullDown pulldown_2 (.out(pc_1_a12[3]));
  Seven_Seg_Hex seven_seg_hex_1 (.d(pc_1_a12), .dp(1'b0));
  LED A12 (.in(pc_1_a12[0]));
  LED A13 (.in(pc_1_a12[1]));
  PullDown pulldown_3 (.out(pc_1_a12[0]));
  PullDown pulldown_4 (.out(pc_1_a12[1]));
  Seven_Seg_Hex seven_seg_hex_2 (.d(pc_1_a8), .dp(1'b0));
  LED A10 (.in(pc_1_a8[2]));
  LED A11 (.in(pc_1_a8[3]));
  PullDown pulldown_5 (.out(pc_1_a8[2]));
  PullDown pulldown_6 (.out(pc_1_a8[3]));
  Seven_Seg_Hex seven_seg_hex_3 (.d(pc_1_a4), .dp(1'b0));
  LED A8 (.in(pc_1_a8[0]));
  LED A9 (.in(pc_1_a8[1]));
  PullDown pulldown_7 (.out(pc_1_a8[0]));
  PullDown pulldown_8 (.out(pc_1_a8[1]));
  Seven_Seg_Hex seven_seg_hex_4 (.d(pc_1_a0), .dp(1'b0));
  LED A6 (.in(pc_1_a4[2]));
  LED A7 (.in(pc_1_a4[3]));
  PullDown pulldown_9 (.out(pc_1_a4[3]));
  PullDown pulldown_10 (.out(pc_1_a4[2]));
  LED A4 (.in(pc_1_a4[0]));
  LED A5 (.in(pc_1_a4[1]));
  PullDown pulldown_11 (.out(pc_1_a4[1]));
  PullDown pulldown_12 (.out(pc_1_a4[0]));
  LED A2 (.in(pc_1_a0[2]));
  LED A3 (.in(pc_1_a0[3]));
  PullDown pulldown_13 (.out(pc_1_a0[3]));
  PullDown pulldown_14 (.out(pc_1_a0[2]));
  LED A0 (.in(pc_1_a0[0]));
  LED A1 (.in(pc_1_a0[1]));
  PullDown pulldown_15 (.out(pc_1_a0[1]));
  PullDown pulldown_16 (.out(pc_1_a0[0]));
  LED D7 (.in(pulldown_20_out[3]));
  PullDown pulldown_17 (.out(pulldown_20_out[3]));
  Seven_Seg_Hex seven_seg_hex_5 (.d(pulldown_20_out), .dp(1'b0));
  LED D5 (.in(pulldown_20_out[1]));
  LED D6 (.in(pulldown_20_out[2]));
  PullDown pulldown_18 (.out(pulldown_20_out[2]));
  PullDown pulldown_19 (.out(pulldown_20_out[1]));
  Seven_Seg_Hex seven_seg_hex_6 (.d(pulldown_24_out), .dp(1'b0));
  LED D3 (.in(pulldown_24_out[3]));
  LED D4 (.in(pulldown_20_out[0]));
  PullDown pulldown_20 (.out(pulldown_20_out[0]));
  PullDown pulldown_21 (.out(pulldown_24_out[3]));
  LED D1 (.in(pulldown_24_out[1]));
  LED D2 (.in(pulldown_24_out[2]));
  PullDown pulldown_22 (.out(pulldown_24_out[2]));
  PullDown pulldown_23 (.out(pulldown_24_out[1]));
  LED D0 (.in(pulldown_24_out[0]));
  PullDown pulldown_24 (.out(pulldown_24_out[0]));
  LED SP_PUSH (.in(pulldown_26_out));
  LED SP_POP (.in(pulldown_25_out));
  PullDown pulldown_25 (.out(pulldown_25_out));
  PullDown pulldown_26 (.out(pulldown_26_out));
  LED SPH_SET (.in(pulldown_28_out));
  LED SPH_OUT (.in(pulldown_27_out));
  PullDown pulldown_27 (.out(pulldown_27_out));
  PullDown pulldown_28 (.out(pulldown_28_out));
  LED SPL_OUT (.in(pulldown_30_out));
  LED SPH_IN (.in(pulldown_29_out));
  PullDown pulldown_29 (.out(pulldown_29_out));
  PullDown pulldown_30 (.out(pulldown_30_out));
  LED SPL_IN (.in(pulldown_32_out));
  LED SPL_SET (.in(pulldown_31_out));
  PullDown pulldown_31 (.out(pulldown_31_out));
  PullDown pulldown_32 (.out(pulldown_32_out));
  LED MPH_SET (.in(pulldown_33_out));
  LED MPH_IN (.in(pulldown_34_out));
  PullDown pulldown_33 (.out(pulldown_33_out));
  PullDown pulldown_34 (.out(pulldown_34_out));
  LED MPL_SET (.in(pulldown_35_out));
  LED MPL_IN (.in(pulldown_36_out));
  PullDown pulldown_35 (.out(pulldown_35_out));
  PullDown pulldown_36 (.out(pulldown_36_out));
  LED C_SET (.in(pulldown_37_out));
  LED C_CLR (.in(pulldown_38_out));
  PullDown pulldown_37 (.out(pulldown_37_out));
  PullDown pulldown_38 (.out(pulldown_38_out));
  LED REGF_OUT (.in(pulldown_39_out));
  LED REGF_SET (.in(pulldown_40_out));
  PullDown pulldown_39 (.out(pulldown_39_out));
  PullDown pulldown_40 (.out(pulldown_40_out));
  LED REGF_IN (.in(pulldown_41_out));
  LED REGS2_OUT (.in(pulldown_42_out));
  PullDown pulldown_41 (.out(pulldown_41_out));
  PullDown pulldown_42 (.out(pulldown_42_out));
  LED REGS2_SET (.in(pulldown_43_out));
  LED REGS2_IN (.in(pulldown_44_out));
  PullDown pulldown_43 (.out(pulldown_43_out));
  PullDown pulldown_44 (.out(pulldown_44_out));
  LED REGS1_OUT (.in(pulldown_45_out));
  LED REGS1_SET (.in(pulldown_46_out));
  PullDown pulldown_45 (.out(pulldown_45_out));
  PullDown pulldown_46 (.out(pulldown_46_out));
  LED REGS1_IN (.in(pulldown_47_out));
  LED REGC_OUT (.in(pulldown_48_out));
  PullDown pulldown_47 (.out(pulldown_47_out));
  PullDown pulldown_48 (.out(pulldown_48_out));
  LED REGC_IN (.in(pulldown_50_out));
  LED REGC_SET (.in(pulldown_49_out));
  PullDown pulldown_49 (.out(pulldown_49_out));
  PullDown pulldown_50 (.out(pulldown_50_out));
  LED REGB_SET (.in(pulldown_52_out));
  LED REGB_OUT (.in(pulldown_51_out));
  PullDown pulldown_51 (.out(pulldown_51_out));
  PullDown pulldown_52 (.out(pulldown_52_out));
  LED REGA_OUT (.in(pulldown_54_out));
  LED REGB_IN (.in(pulldown_53_out));
  PullDown pulldown_53 (.out(pulldown_53_out));
  PullDown pulldown_54 (.out(pulldown_54_out));
  LED REGA_IN (.in(pulldown_56_out));
  LED REGA_SET (.in(pulldown_55_out));
  PullDown pulldown_55 (.out(pulldown_55_out));
  PullDown pulldown_56 (.out(pulldown_56_out));
  LED IRQWAIT_CLR (.in(pulldown_57_out));
  LED IRQSUP_CLR (.in(pulldown_58_out));
  PullDown pulldown_57 (.out(pulldown_57_out));
  PullDown pulldown_58 (.out(pulldown_58_out));
  LED IRQSUP_SET (.in(pulldown_59_out));
  LED IR_SET (.in(pulldown_60_out));
  PullDown pulldown_59 (.out(pulldown_59_out));
  PullDown pulldown_60 (.out(pulldown_60_out));
  LED IR_IN (.in(pulldown_61_out));
  LED MEM_OUT (.in(pulldown_62_out));
  PullDown pulldown_61 (.out(pulldown_61_out));
  PullDown pulldown_62 (.out(pulldown_62_out));
  LED MEN_IN (.in(pulldown_63_out));
  LED PC_OUT (.in(pulldown_64_out));
  PullDown pulldown_63 (.out(pulldown_63_out));
  PullDown pulldown_64 (.out(pulldown_64_out));
  LED PC_SET (.in(pulldown_65_out));
  LED PC_IN (.in(pulldown_66_out));
  PullDown pulldown_65 (.out(pulldown_65_out));
  PullDown pulldown_66 (.out(pulldown_66_out));
  LED PCH_OUT (.in(pulldown_67_out));
  LED PCH_SET (.in(pulldown_68_out));
  PullDown pulldown_67 (.out(pulldown_67_out));
  PullDown pulldown_68 (.out(pulldown_68_out));
  LED PCH_IN (.in(pulldown_69_out));
  LED PCL_OUT (.in(pulldown_70_out));
  PullDown pulldown_69 (.out(pulldown_69_out));
  PullDown pulldown_70 (.out(pulldown_70_out));
  LED PCL_SET (.in(pulldown_71_out));
  LED PCL_IN (.in(pulldown_72_out));
  PullDown pulldown_71 (.out(pulldown_71_out));
  PullDown pulldown_72 (.out(pulldown_72_out));
  LED CLK_CLR (.in(pulldown_73_out));
  PullDown pulldown_73 (.out(pulldown_73_out));
  LED ENABLE (.in(undriven));
  LED LOAD (.in(pulldown_74_out));
  LED CLK (.in(pulldown_75_out));
  PullDown pulldown_74 (.out(pulldown_74_out));
  PullDown pulldown_75 (.out(pulldown_75_out));
  LED RST (.in(pulldown_76_out));
  PullDown pulldown_76 (.out(pulldown_76_out));
  LED A7_2 (.in(rom_1_p1[3]));
  REG8 reg8_1 (
    .D7(mmu_1_p5), .D6(mmu_1_p6), .D5(mmu_1_p7), .D4(mmu_1_p8), .D3(mmu_1_p9), .D2(mmu_1_p10),
    .D1(mmu_1_p11), .D0(mmu_1_p12), .REG_SET(pulldown_74_out), .REG_OUT(pulldown_76_out),
    .REG_IN(decode_1_rega_eout), .REG_CLR(decode_1_rega_ein), .M0(reg8_1_m0), .M1(reg8_1_m1), .M2(reg8_1_m2),
    .M3(reg8_1_m3), .M4(reg8_1_m4), .M5(reg8_1_m5), .M6(reg8_1_m6), .M7(reg8_1_m7));
  // REGA rega_1: pin names not known
  REG8 reg8_2 (
    .D7(mmu_1_p5), .D6(mmu_1_p6), .D5(mmu_1_p7), .D4(mmu_1_p8), .D3(mmu_1_p9), .D2(mmu_1_p10),
    .D1(mmu_1_p11), .D0(mmu_1_p12), .REG_SET(pulldown_74_out), .REG_OUT(pulldown_76_out),
    .REG_IN(decode_1_regb_eout), .REG_CLR(decode_1_regb_ein), .M0(reg8_2_m0), .M1(reg8_2_m1), .M2(reg8_2_m2),
    .M3(reg8_2_m3), .M4(reg8_2_m4), .M5(reg8_2_m5), .M6(reg8_2_m6), .M7(reg8_2_m7));
  // REGA rega_2: pin names not known
  REG8 reg8_3 (
    .D7(mmu_1_p5), .D6(mmu_1_p6), .D5(mmu_1_p7), .D4(mmu_1_p8), .D3(mmu_1_p9), .D2(mmu_1_p10),
    .D1(mmu_1_p11), .D0(mmu_1_p12), .REG_SET(pulldown_74_out), .REG_OUT(pulldown_76_out),
    .REG_IN(decode_1_regs1_eout), .REG_CLR(decode_1_regs1_ein), .M0(reg8_3_m0), .M1(reg8_3_m1),
    .M2(reg8_3_m2), .M3(reg8_3_m3), .M4(reg8_3_m4), .M5(reg8_3_m5), .M6(reg8_3_m6), .M7(reg8_3_m7));
  // REGA rega_3: pin names not known
  REG4 reg4_1 (
    .D3(mmu_1_p9), .D2(mmu_1_p10), .D1(mmu_1_p11), .D0(mmu_1_p12), .REG_SET(pulldown_74_out),
    .REG_OUT(pulldown_76_out), .REG_IN(decode_1_regs2_eout), .REG_CLR(decode_1_regs2_ein), .M0(reg4_1_m0),
    .M1(reg4_1_m1), .M2(reg4_1_m2), .M3(reg4_1_m3));
  Seven_Seg_Hex seven_seg_hex_7 (.d(rom_1_p1), .dp(1'b0));
  LED A6_2 (.in(rom_1_p1[2]));
  LED A5_2 (.in(rom_1_p1[1]));
  Seven_Seg_Hex seven_seg_hex_8 (.d(rom_1_p8), .dp(1'b0));
  LED A4_2 (.in(rom_1_p1[0]));
  LED A3_2 (.in(rom_1_p8[3]));
  LED M7 (.in(reg8_1_m7));
  LED M6 (.in(reg8_1_m6));
  LED M7_2 (.in(reg8_2_m7));
  LED M6_2 (.in(reg8_2_m6));
  LED M7_3 (.in(reg8_3_m7));
  LED M6_3 (.in(reg8_3_m6));
  LED M3 (.in(reg4_1_m3));
  LED M2 (.in(reg4_1_m2));
  // MMU mmu_1: pin names not known; wires that end beside it: pulldown_74_out, pulldown_76_out, mmu_1_p3, mmu_1_p4, mmu_1_p5, mmu_1_p6, mmu_1_p7, mmu_1_p8, mmu_1_p9, mmu_1_p10, mmu_1_p11, mmu_1_p12, mmu_1_p13, mmu_1_p14, mmu_1_p15, mmu_1_p16
  LED A2_2 (.in(rom_1_p8[2]));
  LED A1_2 (.in(rom_1_p8[1]));
  LED M5 (.in(reg8_1_m5));
  LED M4 (.in(reg8_1_m4));
  LED M5_2 (.in(reg8_2_m5));
  LED M4_2 (.in(reg8_2_m4));
  LED F (.in(reg8_3_m5));
  LED M (.in(reg8_3_m4));
  LED M1 (.in(reg4_1_m1));
  LED CIN (.in(reg4_1_m0));
  LED A0_2 (.in(rom_1_p8[0]));
  // ROM rom_1: pin names not known; wires that end beside it: rom_1_p1[3], rom_1_p1[2], rom_1_p1[1], rom_1_p1[3], rom_1_p1[2], rom_1_p1[1], rom_1_p1[0], rom_1_p8[3], rom_1_p8[2], rom_1_p8[1], rom_1_p8[0], rom_1_p12, rom_1_p13, rom_1_p17[3], rom_1_p17[2], rom_1_p17[1], rom_1_p17[0], rom_1_p21[3], rom_1_p21[2], rom_1_p21[1], rom_1_p21[0], mmu_1_p5, mmu_1_p6, mmu_1_p7, mmu_1_p8, mmu_1_p9, mmu_1_p10, mmu_1_p11, mmu_1_p12, rom_1_p30, rom_1_p31, rom_1_p32, rom_1_p33, rom_1_p34, rom_1_p35, rom_1_p36, rom_1_p37
  LED M3_2 (.in(reg8_1_m3));
  LED M2_2 (.in(reg8_1_m2));
  LED M3_3 (.in(reg8_2_m3));
  LED M2_3 (.in(reg8_2_m2));
  LED S3 (.in(reg8_3_m3));
  LED S2 (.in(reg8_3_m2));
  LED M1_2 (.in(reg8_1_m1));
  LED M0 (.in(reg8_1_m0));
  LED M0_2 (.in(reg8_2_m0));
  LED M1_3 (.in(reg8_2_m1));
  LED S1 (.in(reg8_3_m1));
  LED S0 (.in(reg8_3_m0));
  Seven_Seg_Hex seven_seg_hex_9 (.d(rom_1_p17), .dp(1'b0));
  Seven_Seg_Hex seven_seg_hex_10 (.d(rom_1_p21), .dp(1'b0));
  ALU alu_1 (
    .A0(reg8_1_m0), .A1(reg8_1_m1), .A2(reg8_1_m2), .A3(reg8_1_m3), .A4(reg8_1_m4), .A5(reg8_1_m5),
    .A6(reg8_1_m6), .A7(reg8_1_m7), .B0(reg8_2_m0), .B1(reg8_2_m1), .B2(reg8_2_m2), .B3(reg8_2_m3),
    .B4(reg8_2_m4), .B5(reg8_2_m5), .B6(reg8_2_m6), .B7(reg8_2_m7), .S0(reg8_3_m0), .S1(reg8_3_m1),
    .S2(reg8_3_m2), .S3(reg8_3_m3), .M(reg8_3_m4), .CIN(reg4_1_m0), .F(reg8_3_m5), .C0(alu_1_c0),
    .C1(alu_1_c1), .C2(alu_1_c2), .C3(alu_1_c3), .C4(alu_1_c4), .C5(alu_1_c5), .C6(alu_1_c6), .C7(alu_1_c7),
    .Z(alu_1_z), .EQ(alu_1_eq), .COUT(alu_1_cout));
  LED C7 (.in(alu_1_c7));
  LED C6 (.in(alu_1_c6));
  LED C5 (.in(alu_1_c5));
  LED C4 (.in(alu_1_c4));
  LED C3 (.in(alu_1_c3));
  Seven_Seg_Hex seven_seg_hex_11 (.d(undriven_3[7:4]), .dp(1'b0));
  DECODE decode_1 (
    .A7(rom_1_p17[3]), .A6(rom_1_p17[2]), .A5(rom_1_p17[1]), .A4(rom_1_p17[0]), .A3(rom_1_p21[3]),
    .A2(rom_1_p21[2]), .A1(rom_1_p21[1]), .A0(rom_1_p21[0]), .ROM_EDOUT(rom_1_p12), .PC_EIN(decode_1_pc_ein),
    .REGF2_EOUT(decode_1_regf2_eout), .REGF2_EIN(decode_1_regf2_ein), .REGF1_EOUT(decode_1_regf1_eout),
    .REGF1_EIN(decode_1_regf1_ein), .REGS2_EOUT(decode_1_regs2_eout), .REGS2_EIN(decode_1_regs2_ein),
    .PC_EOUT(decode_1_pc_eout), .ROM_EAOUT(rom_1_p13), .STK_EOUT(decode_1_stk_eout), .MEMAH_EIN(mmu_1_p3),
    .MEMAL_EIN(mmu_1_p4), .MEM_EOUT(mmu_1_p13), .MEM_EIN(mmu_1_p14), .REGS1_EOUT(decode_1_regs1_eout),
    .REGS1_EIN(decode_1_regs1_ein), .REGC_EOUT(decode_1_regc_eout), .REGC_EIN(decode_1_regc_ein),
    .REGB_EOUT(decode_1_regb_eout), .REGB_EIN(decode_1_regb_ein), .REGA_EOUT(decode_1_rega_eout),
    .REGA_EIN(decode_1_rega_ein), .C(undriven_16), .Z(undriven_15), .EQ(undriven_12), .SWP(undriven_10),
    .S0(decode_1_s0), .S1(decode_1_s1), .S2(decode_1_s2), .RST(decode_1_rst), .ENABLE(undriven),
    .P0(decode_1_p0), .P1(decode_1_p1), .P2(decode_1_p2), .PG(mmu_1_p16), .INC(mmu_1_p15), .S3(decode_1_s3),
    .HALT(decode_1_halt), .SPARE4(undriven_3), .NEG(1'b0), .OVR(1'b0), .IRQ(undriven_2), .SPARE1(1'b0),
    .SPARE2(1'b0), .SPARE3(1'b0));  // open: IV_EIN, IV_EOUT, IRQ_ON, IRQ_OFF, IRQ_SUP_ON, IRQ_SUP_OFF
  LED C2 (.in(alu_1_c2));
  LED C1 (.in(alu_1_c1));
  Seven_Seg_Hex seven_seg_hex_12 (.d(undriven_3[3:0]), .dp(1'b0));
  LED C0 (.in(alu_1_c0));
  LED EQ (.in(alu_1_eq));
  LED Z (.in(alu_1_z));
  LED COUT (.in(alu_1_cout));
  LED M7_4 (.in(undriven_4));
  LED M6_4 (.in(undriven_7));
  LED M5_3 (.in(undriven_11));
  LED M3_4 (.in(undriven_5));
  LED M2_4 (.in(undriven_8));
  LED M3_5 (.in(undriven_6));
  LED M2_5 (.in(undriven_9));
  LED M4_3 (.in(undriven_14));
  LED M3_6 (.in(undriven_17));
  LED EQ_2 (.in(undriven_12));
  LED Z_2 (.in(undriven_15));
  LED M1_4 (.in(undriven_13));
  LED COUT_2 (.in(undriven_16));
  LED M2_6 (.in(undriven_18));
  LED M1_5 (.in(undriven_19));
  LED M0_3 (.in(undriven_20));

  // Notes on the sheet:
  //   Address
  //   Data
  //   Instruction
  //   Address
  //   Instruction
  //   Actual Instruction
endmodule
