// Digital circuit CPU_TEST.dig as structural Verilog
module CPU_TEST (
  input  clk,
  input  POP,
  input  PUSH,
  input  LOAD,
  input  EIN,
  input  EOUT,
  input  CLR,
  input  D0,
  input  DN,
  input  UP,
  input  D1,
  input  D2,
  input  D3,
  input  CLR_2,
  input  nLD,
  input  VCC,
  input  GND,
  output Q4,
  output Q3,
  output Q1,
  output Q0,
  output ERR,
  output nBO,
  output nCO,
  output Q0_2,
  output Q1_2,
  output Q2,
  output Q3_2
);

  wire alu_1_c0, alu_1_c1, alu_1_c2, alu_1_c3, alu_1_c4, alu_1_c5, alu_1_c6, alu_1_c7, alu_1_cout, alu_1_eq,
       alu_1_z, and_1_out, and_2_out, and_3_out, and_4_out, and_5_out, and_6_out, and_7_out, and_8_out,
       and_9_out, and_10_out, clk_1_p2, clk_1_p3, clk_1_p4, clk_1_p6, clk_1_p7, clk_1_p8, clk_1_p9,
       clk_1_p10, clk_1_p11, clk_1_p12, clk_1_p13, clk_1_p14, clk_1_p15, clk_1_p16, clk_1_p17, clk_1_p18,
       clk_1_p19, clk_1_p20, clk_1_p21, clk_1_p22, clk_1_p23, decode_1_mem_ein, decode_1_mem_eout,
       decode_1_memah_ein, decode_1_memal_ein, decode_1_regc_ein, decode_1_regc_eout, decode_1_regf1_ein,
       decode_1_regf1_eout, decode_1_regf2_ein, decode_1_regf2_eout, decode_1_regs2_ein, decode_1_regs2_eout,
       decode_1_rom_eaout, decode_1_rst, decode_1_stk_eout, jk_ff_as_1_nq, jk_ff_as_2_nq, jk_ff_as_3_nq,
       jk_ff_as_4_nq, nand_1_out, nand_2_out, nand_3_out, nand_4_out, nand_7_out, nand_8_out, nand_9_out,
       nand_10_out, nor_1_out, not_1_out, not_2_out, not_3_out, not_4_out, not_5_out, not_6_out, not_7_out,
       not_8_out, not_9_out, not_10_out, not_11_out, not_12_out, not_13_out, not_14_out, or_1_out, or_2_out,
       or_3_out, or_4_out, or_5_out, or_6_out, or_7_out, or_8_out, or_9_out, pc_1_p9, pc_1_p12, REG_A_p11,
       REG_A_p12, REG_A_p13, REG_A_p14, REG_A_p15, REG_A_p16, REG_A_p17, REG_A_p18, REG_A_p19, REG_A_p20,
       REG_B_p11, REG_B_p12, REG_B_p13, REG_B_p14, REG_B_p15, REG_B_p16, REG_B_p17, REG_B_p18, REG_B_p19,
       REG_B_p20, REG_C_m0, REG_C_m1, REG_C_m2, REG_C_m3, REG_C_m4, REG_C_m5, REG_C_m6, REG_C_m7, REG_F1_m0,
       REG_F1_m1, REG_F1_m2, REG_F1_m3, REG_F2_m0, REG_F2_m1, REG_F2_m2, REG_F2_m3, REG_S1_p11, REG_S1_p12,
       REG_S1_p13, REG_S1_p14, REG_S1_p15, REG_S1_p16, REG_S1_p17, REG_S1_p18, REG_S1_p19, REG_S1_p20,
       REG_S2_m0, REG_S2_m1, REG_S2_m2, REG_S2_m3, rom_1_p9, rom_1_p10, rom_1_p11, rom_1_p12, rom_1_p13,
       rom_1_p14, rom_1_p15, rom_1_p16, rom_1_p17, switch_2_b;
  wire [3:0] pc_1_p16, pc_1_p20;
  wire [7:0] blockramdualport_1_d, driver_8_out;

  not not_1 (not_1_out, DN);
  not not_2 (not_2_out, UP);
  not not_3 (not_3_out, CLR_2);
  not not_4 (not_4_out, nLD);
  PowerSupply powersupply_1 (.VDD(VCC), .GND(GND));
  nand nand_1 (nand_1_out, D0, not_4_out, not_3_out);
  nand nand_2 (nand_2_out, D1, not_4_out, not_3_out);
  and and_1 (and_1_out, not_1_out, jk_ff_as_1_nq);
  and and_2 (and_2_out, Q0_2, not_2_out);
  nand nand_3 (nand_3_out, D2, not_4_out, not_3_out);
  and and_3 (and_3_out, not_1_out, jk_ff_as_1_nq, jk_ff_as_2_nq);
  and and_4 (and_4_out, Q0_2, Q1_2, not_2_out);
  nand nand_4 (nand_4_out, D3, not_4_out, not_3_out);
  and and_5 (and_5_out, not_1_out, jk_ff_as_1_nq, jk_ff_as_2_nq, jk_ff_as_3_nq);
  and and_6 (and_6_out, Q0_2, Q1_2, Q2, not_2_out);
  nand nand_5 (nBO, not_1_out, jk_ff_as_1_nq, jk_ff_as_2_nq, jk_ff_as_3_nq, jk_ff_as_4_nq);
  nand nand_6 (nCO, Q0_2, Q1_2, Q2, Q3_2, not_2_out);
  or or_1 (or_1_out, not_1_out, not_2_out);
  or or_2 (or_2_out, and_1_out, and_2_out);
  or or_3 (or_3_out, and_3_out, and_4_out);
  or or_4 (or_4_out, and_5_out, and_6_out);
  nand nand_7 (nand_7_out, nand_1_out, not_4_out);
  nand nand_8 (nand_8_out, nand_2_out, not_4_out);
  nand nand_9 (nand_9_out, nand_3_out, not_4_out);
  nand nand_10 (nand_10_out, nand_4_out, not_4_out);
  // _74193 _74193_1: pin names not known
  not not_5 (not_5_out, or_1_out);
  or or_5 (or_5_out, ~not_3_out, ~nand_7_out);  // Or
  not not_6 (not_6_out, or_2_out);
  or or_6 (or_6_out, ~not_3_out, ~nand_8_out);  // Or
  not not_7 (not_7_out, or_3_out);
  or or_7 (or_7_out, ~not_3_out, ~nand_9_out);  // Or
  not not_8 (not_8_out, or_4_out);
  or or_8 (or_8_out, ~not_3_out, ~nand_10_out);  // Or
  not not_9 (not_9_out, nand_1_out);
  JK_FF_AS jk_ff_as_1 (
    .Set(not_9_out), .J(1'b1), .C(not_5_out), .K(1'b1), .Clr(or_5_out), .Q(Q0_2), .nQ(jk_ff_as_1_nq));
  not not_10 (not_10_out, nand_2_out);
  JK_FF_AS jk_ff_as_2 (
    .Set(not_10_out), .J(1'b1), .C(not_6_out), .K(1'b1), .Clr(or_6_out), .Q(Q1_2), .nQ(jk_ff_as_2_nq));
  not not_11 (not_11_out, nand_3_out);
  JK_FF_AS jk_ff_as_3 (.Set(not_11_out), .J(1'b1), .C(not_7_out), .K(1'b1), .Clr(or_7_out), .Q(Q2), .nQ(jk_ff_as_3_nq));
  not not_12 (not_12_out, nand_4_out);
  JK_FF_AS jk_ff_as_4 (
    .Set(not_12_out), .J(1'b1), .C(not_8_out), .K(1'b1), .Clr(or_8_out), .Q(Q3_2), .nQ(jk_ff_as_4_nq));
  not not_13 (not_13_out, clk_1_p21);
  not not_14 (not_14_out, clk_1_p20);
  Switch switch_1 (.A(1'b1), .B(clk));
  PullDown pulldown_1 (.out(clk));
  or or_9 (or_9_out, decode_1_rom_eaout, decode_1_stk_eout);
  BlockRAMDualPort #(.AddrBits(4), .Bits(8)) blockramdualport_1 (
    .A({Q4, Q3, Q1, Q0}), .Din(driver_8_out), .str(or_9_out), .C(and_7_out), .D(blockramdualport_1_d));
  and and_7 (and_7_out, decode_1_stk_eout, clk_1_p8);
  // CLK clk_1: pin names not known; wires that end beside it: clk, clk_1_p2, clk_1_p3, clk_1_p4, ERR, clk_1_p6, clk_1_p7, clk_1_p8, clk_1_p9, clk_1_p10, clk_1_p11, clk_1_p12, clk_1_p13, clk_1_p14, clk_1_p15, clk_1_p16, clk_1_p17, clk_1_p18, clk_1_p19, clk_1_p20, clk_1_p21, clk_1_p22, clk_1_p23
  and and_8 (and_8_out, 1'b1, and_9_out);
  and and_9 (and_9_out, Q4, Q3, Q1, Q0);
  and and_10 (and_10_out, clk_1_p21, nor_1_out);
  nor nor_1 (nor_1_out, Q4, Q3, Q1, Q0);
  LED led_1 (.in(clk_1_p19));
  LED led_2 (.in(clk_1_p18));
  LED led_3 (.in(clk_1_p17));
  LED led_4 (.in(clk_1_p16));
  LED led_5 (.in(clk_1_p15));
  LED led_6 (.in(clk_1_p14));
  LED led_7 (.in(clk_1_p13));
  LED led_8 (.in(clk_1_p12));
  LED led_9 (.in(clk_1_p11));
  LED led_10 (.in(clk_1_p10));
  or or_10 (ERR, and_10_out, and_8_out);
  assign driver_8_out[7] = decode_1_rom_eaout ? blockramdualport_1_d[0] : 1'bz;  // Driver driver_1
  assign driver_8_out[6] = decode_1_rom_eaout ? blockramdualport_1_d[1] : 1'bz;  // Driver driver_2
  assign driver_8_out[5] = decode_1_rom_eaout ? blockramdualport_1_d[2] : 1'bz;  // Driver driver_3
  assign driver_8_out[4] = decode_1_rom_eaout ? blockramdualport_1_d[3] : 1'bz;  // Driver driver_4
  assign driver_8_out[3] = decode_1_rom_eaout ? blockramdualport_1_d[4] : 1'bz;  // Driver driver_5
  assign driver_8_out[2] = decode_1_rom_eaout ? blockramdualport_1_d[5] : 1'bz;  // Driver driver_6
  assign driver_8_out[1] = decode_1_rom_eaout ? blockramdualport_1_d[6] : 1'bz;  // Driver driver_7
  assign driver_8_out[0] = decode_1_rom_eaout ? blockramdualport_1_d[7] : 1'bz;  // Driver driver_8
  Switch switch_2 (.A(1'b1), .B(switch_2_b));
  or or_11 (clk_1_p6, decode_1_rst, switch_2_b);
  PullDown pulldown_2 (.out(switch_2_b));
  LED led_11 (.in(Q4));
  LED led_12 (.in(Q3));
  LED led_13 (.in(Q1));
  LED led_14 (.in(Q0));
  LED D6 (.in(driver_8_out[1]));
  LED D7 (.in(driver_8_out[0]));
  PullDown pulldown_3 (.out(driver_8_out[0]));
  PullDown pulldown_4 (.out(driver_8_out[1]));
  LED D4 (.in(driver_8_out[3]));
  LED D5 (.in(driver_8_out[2]));
  PullDown pulldown_5 (.out(driver_8_out[2]));
  PullDown pulldown_6 (.out(driver_8_out[3]));
  LED u_D2 (.in(driver_8_out[5]));
  LED u_D3 (.in(driver_8_out[4]));
  PullDown pulldown_7 (.out(driver_8_out[4]));
  PullDown pulldown_8 (.out(driver_8_out[5]));
  LED u_D0 (.in(driver_8_out[7]));
  LED u_D1 (.in(driver_8_out[6]));
  PullDown pulldown_9 (.out(driver_8_out[6]));
  PullDown pulldown_10 (.out(driver_8_out[7]));
  LED ENABLE (.in(clk_1_p9));
  LED u_LOAD (.in(clk_1_p8));
  PullDown pulldown_11 ();  // open: out
  PullDown pulldown_12 (.out(clk_1_p8));
  LED CLK_2 (.in(clk_1_p7));
  LED RST (.in(clk_1_p6));
  PullDown pulldown_13 (.out(clk_1_p7));
  PullDown pulldown_14 (.out(clk_1_p6));
  // PC pc_1: pin names not known; wires that end beside it: driver_8_out[0], driver_8_out[1], driver_8_out[2], driver_8_out[3], driver_8_out[4], driver_8_out[5], driver_8_out[6], driver_8_out[7], pc_1_p9, clk_1_p7, clk_1_p6, pc_1_p12, pc_1_p16[3], pc_1_p16[2], pc_1_p16[1], pc_1_p16[0], pc_1_p20[3], pc_1_p20[2], pc_1_p20[1], pc_1_p20[0]
  Seven_Seg_Hex seven_seg_hex_1 (.d(pc_1_p16), .dp(1'b0));
  LED A7 (.in(pc_1_p16[3]));
  LED A6 (.in(pc_1_p16[2]));
  // Register8 REG_A: pin names not known; wires that end beside it: driver_8_out[0], driver_8_out[1], driver_8_out[2], driver_8_out[3], driver_8_out[4], driver_8_out[5], driver_8_out[6], driver_8_out[7], clk_1_p8, clk_1_p6, REG_A_p11, REG_A_p12, REG_A_p13, REG_A_p14, REG_A_p15, REG_A_p16, REG_A_p17, REG_A_p18, REG_A_p19, REG_A_p20
  // Register8 REG_B: pin names not known; wires that end beside it: driver_8_out[0], driver_8_out[1], driver_8_out[2], driver_8_out[3], driver_8_out[4], driver_8_out[5], driver_8_out[6], driver_8_out[7], clk_1_p8, clk_1_p6, REG_B_p11, REG_B_p12, REG_B_p13, REG_B_p14, REG_B_p15, REG_B_p16, REG_B_p17, REG_B_p18, REG_B_p19, REG_B_p20
  // Register8 REG_S1: pin names not known; wires that end beside it: driver_8_out[0], driver_8_out[1], driver_8_out[2], driver_8_out[3], driver_8_out[4], driver_8_out[5], driver_8_out[6], driver_8_out[7], clk_1_p8, clk_1_p6, REG_S1_p11, REG_S1_p12, REG_S1_p13, REG_S1_p14, REG_S1_p15, REG_S1_p16, REG_S1_p17, REG_S1_p18, REG_S1_p19, REG_S1_p20
  Register4 REG_S2 (
    .D3(driver_8_out[4]), .D2(driver_8_out[5]), .D1(driver_8_out[6]), .D0(driver_8_out[7]), .LOAD(clk_1_p8),
    .RST(clk_1_p6), .EOUT(decode_1_regs2_eout), .EIN(decode_1_regs2_ein), .M0(REG_S2_m0), .M1(REG_S2_m1),
    .M2(REG_S2_m2), .M3(REG_S2_m3));
  MemoryManager memorymanager_1 (
    .D7(driver_8_out[0]), .D6(driver_8_out[1]), .D5(driver_8_out[2]), .D4(driver_8_out[3]),
    .D3(driver_8_out[4]), .D2(driver_8_out[5]), .D1(driver_8_out[6]), .D0(driver_8_out[7]),
    .EIN_L(decode_1_memal_ein), .LOAD(clk_1_p8), .RST(clk_1_p6), .EIN_H(decode_1_memah_ein),
    .EOUT(decode_1_mem_eout), .EIN(decode_1_mem_ein));  // open: PG, P2, A7, A6, A5, A4, A3, A2, A1, A0, INC, P1, P0
  Seven_Seg_Hex seven_seg_hex_2 (.d(pc_1_p20), .dp(1'b0));
  LED A5 (.in(pc_1_p16[1]));
  LED A4 (.in(pc_1_p16[0]));
  LED M7 (.in(REG_A_p20));
  LED M7_2 (.in(REG_B_p20));
  LED M7_3 (.in(REG_S1_p20));
  LED M3 (.in(REG_S2_m3));
  LED A3 (.in(pc_1_p20[3]));
  LED A2 (.in(pc_1_p20[2]));
  LED M6 (.in(REG_A_p19));
  LED M5 (.in(REG_A_p18));
  LED M6_2 (.in(REG_B_p19));
  LED M5_2 (.in(REG_B_p18));
  LED M6_3 (.in(REG_S1_p19));
  LED M5_3 (.in(REG_S1_p18));
  LED M2 (.in(REG_S2_m2));
  LED M1 (.in(REG_S2_m1));
  LED A1 (.in(pc_1_p20[1]));
  LED A0 (.in(pc_1_p20[0]));
  // ROM rom_1: pin names not known; wires that end beside it: pc_1_p16[3], pc_1_p16[2], pc_1_p16[1], pc_1_p16[0], pc_1_p20[3], pc_1_p20[2], pc_1_p20[1], pc_1_p20[0], rom_1_p9, rom_1_p10, rom_1_p11, rom_1_p12, rom_1_p13, rom_1_p14, rom_1_p15, rom_1_p16, rom_1_p17, driver_8_out[0], driver_8_out[1], driver_8_out[2], driver_8_out[3], driver_8_out[4], driver_8_out[5], driver_8_out[6], driver_8_out[7]
  LED M4 (.in(REG_A_p17));
  LED M3_2 (.in(REG_A_p16));
  LED M4_2 (.in(REG_B_p17));
  LED M3_3 (.in(REG_B_p16));
  LED M4_3 (.in(REG_S1_p17));
  LED M3_4 (.in(REG_S1_p16));
  LED CIN (.in(REG_S2_m0));
  LED M2_2 (.in(REG_A_p15));
  LED M1_2 (.in(REG_A_p14));
  LED M2_3 (.in(REG_B_p15));
  LED M1_3 (.in(REG_B_p14));
  LED M1_4 (.in(REG_S1_p14));
  LED M2_4 (.in(REG_S1_p15));
  LED M0 (.in(REG_A_p13));
  LED M0_2 (.in(REG_B_p13));
  LED M0_3 (.in(REG_S1_p13));
  ALU alu_1 (
    .A0(REG_A_p13), .A1(REG_A_p14), .A2(REG_A_p15), .A3(REG_A_p16), .A4(REG_A_p17), .A5(REG_A_p18),
    .A6(REG_A_p19), .A7(REG_A_p20), .B0(REG_B_p13), .B1(REG_B_p14), .B2(REG_B_p15), .B3(REG_B_p16),
    .B4(REG_B_p17), .B5(REG_B_p18), .B6(REG_B_p19), .B7(REG_B_p20), .S0(REG_S1_p13), .S1(REG_S1_p14),
    .S2(REG_S1_p15), .S3(REG_S1_p16), .M(REG_S1_p17), .CIN(REG_S2_m0), .C0(alu_1_c0), .C1(alu_1_c1),
    .C2(alu_1_c2), .C3(alu_1_c3), .C4(alu_1_c4), .C5(alu_1_c5), .C6(alu_1_c6), .C7(alu_1_c7), .Z(alu_1_z),
    .EQ(alu_1_eq), .COUT(alu_1_cout));  // open: F
  DECODE decode_1 (
    .A7(rom_1_p10), .A6(rom_1_p11), .A5(rom_1_p12), .A4(rom_1_p13), .A3(rom_1_p14), .A2(rom_1_p15),
    .A1(rom_1_p16), .A0(rom_1_p17), .ROM_EDOUT(rom_1_p9), .PC_EIN(pc_1_p9), .REGF2_EOUT(decode_1_regf2_eout),
    .REGF2_EIN(decode_1_regf2_ein), .REGF1_EOUT(decode_1_regf1_eout), .REGF1_EIN(decode_1_regf1_ein),
    .REGS2_EOUT(decode_1_regs2_eout), .REGS2_EIN(decode_1_regs2_ein), .PC_EOUT(pc_1_p12),
    .ROM_EAOUT(decode_1_rom_eaout), .STK_EOUT(decode_1_stk_eout), .MEMAH_EIN(decode_1_memah_ein),
    .MEMAL_EIN(decode_1_memal_ein), .MEM_EOUT(decode_1_mem_eout), .MEM_EIN(decode_1_mem_ein),
    .REGS1_EOUT(REG_S1_p11), .REGS1_EIN(REG_S1_p12), .REGC_EOUT(decode_1_regc_eout),
    .REGC_EIN(decode_1_regc_ein), .REGB_EOUT(REG_B_p11), .REGB_EIN(REG_B_p12), .REGA_EOUT(REG_A_p11),
    .REGA_EIN(REG_A_p12), .C(REG_F2_m0), .Z(REG_F1_m0), .EQ(REG_F1_m1), .S0(clk_1_p22), .S1(clk_1_p4),
    .S2(clk_1_p3), .RST(decode_1_rst), .ENABLE(clk_1_p9), .S3(clk_1_p2));  // open: SWP, P0, P1, P2, PG, INC, IV_EIN, IV_EOUT, IRQ_ON, IRQ_OFF, IRQ_SUP_ON, IRQ_SUP_OFF, HALT, SPARE4, NEG, OVR, IRQ, SPARE1, SPARE2, SPARE3
  LED C7 (.in(alu_1_c7));
  LED C6 (.in(alu_1_c6));
  LED C5 (.in(alu_1_c5));
  LED C4 (.in(alu_1_c4));
  LED C3 (.in(alu_1_c3));
  LED C2 (.in(alu_1_c2));
  LED C1 (.in(alu_1_c1));
  LED C0 (.in(alu_1_c0));
  LED Z (.in(alu_1_z));
  LED COUT (.in(alu_1_cout));
  LED EQ (.in(alu_1_eq));
  Register_SepOut8 REG_C (
    .D7(alu_1_c7), .D6(alu_1_c6), .D5(alu_1_c5), .D4(alu_1_c4), .D3(alu_1_c3), .D2(alu_1_c2), .D1(alu_1_c1),
    .D0(alu_1_c0), .LOAD(clk_1_p8), .RST(clk_1_p6), .EOUT(decode_1_regc_eout), .EIN(decode_1_regc_ein),
    .M0(REG_C_m0), .M1(REG_C_m1), .M2(REG_C_m2), .M3(REG_C_m3), .M4(REG_C_m4), .M5(REG_C_m5), .M6(REG_C_m6),
    .M7(REG_C_m7), .Q7(driver_8_out[0]), .Q6(driver_8_out[1]), .Q5(driver_8_out[2]), .Q4(driver_8_out[3]),
    .Q3(driver_8_out[4]), .Q2(driver_8_out[5]), .Q1(driver_8_out[6]), .Q0(driver_8_out[7]));
  Register_SepOut4 REG_F1 (
    .D3(1'b0), .D2(1'b0), .D1(alu_1_eq), .D0(alu_1_z), .LOAD(clk_1_p8), .RST(clk_1_p6),
    .EOUT(decode_1_regf1_eout), .EIN(decode_1_regf1_ein), .M0(REG_F1_m0), .M1(REG_F1_m1), .M2(REG_F1_m2),
    .M3(REG_F1_m3), .Q3(driver_8_out[4]), .Q2(driver_8_out[5]), .Q1(driver_8_out[6]), .Q0(driver_8_out[7]));
  Register_SepOut4 REG_F2 (
    .D3(1'b0), .D2(1'b0), .D1(1'b0), .D0(alu_1_cout), .LOAD(clk_1_p8), .RST(clk_1_p6),
    .EOUT(decode_1_regf2_eout), .EIN(decode_1_regf2_ein), .M0(REG_F2_m0), .M1(REG_F2_m1), .M2(REG_F2_m2),
    .M3(REG_F2_m3), .Q3(driver_8_out[4]), .Q2(driver_8_out[5]), .Q1(driver_8_out[6]), .Q0(driver_8_out[7]));
  LED M7_4 (.in(REG_C_m7));
  LED M6_4 (.in(REG_C_m6));
  LED M3_5 (.in(REG_F1_m3));
  LED M2_5 (.in(REG_F1_m2));
  LED M3_6 (.in(REG_F2_m3));
  LED M2_6 (.in(REG_F2_m2));
  LED M5_4 (.in(REG_C_m5));
  LED M4_4 (.in(REG_C_m4));
  LED EQ_2 (.in(REG_F1_m1));
  LED Z_2 (.in(REG_F1_m0));
  LED M1_5 (.in(REG_F2_m1));
  LED COUT_2 (.in(REG_F2_m0));
  LED M3_7 (.in(REG_C_m3));
  LED M2_7 (.in(REG_C_m2));
  LED M1_6 (.in(REG_C_m1));
  LED M0_4 (.in(REG_C_m0));

  // Notes on the sheet:
  //   nBO: Borrow Output, pin 13
  //   nCO: Carry Output, pin 12
  //   D0: Data Input 0, pin 15
  //   DN: Down Count, pin 4
  //   UP: Up Count, pin 5
  //   Q0_2: Output Q0, pin 3
  //   Q1_2: Output Q1, pin 2
  //   D1: Data Input 1, pin 1
  //   Q2: Output Q2, pin 6
  //   D2: Data Input 2, pin 10
  //   Q3_2: Output Q3, pin 7
  //   D3: Data Input 3, pin 9
  //   CLR_2: Clear, pin 14
  //   nLD: Load, pin 11
  //   VCC: pin 16, default 1
  //   GND: pin 8
  //   Past TOS
  //   Past BOS
endmodule

/* Test case Count:
CLR ~LD D0 D1 D2 D3 UP DN Q0 Q1 Q2 Q3 ~CO ~BO
0 1 0 0 0 0 1 1 X X X X 1 1
0 1 1 0 1 1 1 1 X X X X 1 1
1 1 1 0 1 1 1 1 0 0 0 0 1 1
0 1 1 0 1 1 1 1 0 0 0 0 1 1
0 0 1 0 1 1 1 1 1 0 1 1 1 1
0 1 X X X X 1 1 1 0 1 1 1 1
0 1 X X X X 0 1 1 0 1 1 1 1
0 1 X X X X 1 1 0 1 1 1 1 1
0 1 X X X X 0 1 0 1 1 1 1 1
0 1 X X X X 1 1 1 1 1 1 1 1
0 1 X X X X 0 1 1 1 1 1 0 1
0 1 X X X X 1 1 0 0 0 0 1 1
0 1 X X X X 0 1 0 0 0 0 1 1
0 1 X X X X 1 1 1 0 0 0 1 1
0 1 X X X X 0 1 1 0 0 0 1 1
0 1 X X X X 1 1 0 1 0 0 1 1
0 1 X X X X 1 0 0 1 0 0 1 1
0 1 X X X X 1 1 1 0 0 0 1 1
0 1 X X X X 1 0 1 0 0 0 1 1
0 1 X X X X 1 1 0 0 0 0 1 1
0 1 X X X X 1 0 0 0 0 0 1 0
0 1 X X X X 1 1 1 1 1 1 1 1
0 1 X X X X 1 0 1 1 1 1 1 1
0 1 X X X X 1 1 0 1 1 1 1 1
0 1 X X X X 1 0 0 1 1 1 1 1
0 1 X X X X 1 1 1 0 1 1 1 1
*/
