// Digital circuit DECODE.dig as structural Verilog
module DECODE (
  input  A7,
  input  A6,
  input  A5,
  input  A4,
  input  A3,
  input  A2,
  input  A1,
  input  A0,
  input  C,
  input  Z,
  input  EQ,
  input  SWP,
  input  ENABLE,
  input  [7:0] SPARE4,
  input  NEG,
  input  OVR,
  input  IRQ,
  input  SPARE1,
  input  SPARE2,
  input  SPARE3,
  output ROM_EDOUT,
  output PC_EIN,
  output REGF2_EOUT,
  output REGF2_EIN,
  output REGF1_EOUT,
  output REGF1_EIN,
  output REGS2_EOUT,
  output REGS2_EIN,
  output PC_EOUT,
  output ROM_EAOUT,
  output STK_EOUT,
  output MEMAH_EIN,
  output MEMAL_EIN,
  output MEM_EOUT,
  output MEM_EIN,
  output REGS1_EOUT,
  output REGS1_EIN,
  output REGC_EOUT,
  output REGC_EIN,
  output REGB_EOUT,
  output REGB_EIN,
  output REGA_EOUT,
  output REGA_EIN,
  output S0,
  output S1,
  output S2,
  output RST,
  output P0,
  output P1,
  output P2,
  output PG,
  output INC,
  output IV_EIN,
  output IV_EOUT,
  output IRQ_ON,
  output IRQ_OFF,
  output IRQ_SUP_ON,
  output IRQ_SUP_OFF,
  output S3,
  output HALT
);

  wire _7405a_1__1y, _7405a_1__2y, _7405a_1__4y, _7405a_2__1y, _7405a_2__2y, _7405a_2__3y, _7405a_3__1y,
       _7405a_3__2y, _7405a_3__3y, _7405a_3__4y, _7405a_3__5y, _7408_1_pin3, _7408_1_pin6, _7408_2_pin3,
       _7408_2_pin6, _7421_1_pin6, _7430_1_pin4, _7430_1_pin8, _7430_2_pin8, _7430_3_pin8, _7430_4_pin8,
       _7430_5_pin8, _7432_1_pin3, _7432_1_pin6, _7432_1_pin8, _7432_1_pin11, _7432_3_pin3, _7432_3_pin6,
       or_1_out;
  wire [3:0] _7432_2_pin6, _7432_3_pin8;

  _7405A _7405a_1 (
    ._1A(ENABLE), ._1Y(_7405a_1__1y), ._2A(IRQ), ._2Y(_7405a_1__2y), ._3A(1'b0), ._4A(_7430_1_pin4),
    ._4Y(_7405a_1__4y), ._5A(1'b0), ._6A(1'b0), .VCC(1'b1), .GND(1'b0));  // open: _3Y, _5Y, _6Y
  or or_1 (or_1_out, A0, SWP);
  _7408 _7408_1 (
    .pin1(IRQ), .pin2(SWP), .pin3(_7408_1_pin3), .pin4(_7405a_1__4y), .pin5(or_1_out), .pin6(_7408_1_pin6),
    .pin7(1'b0), .pin9(1'b0), .pin10(1'b0), .pin12(1'b0), .pin13(1'b0), .pin14(1'b1));  // open: pin8, pin11
  _7405A _7405a_2 (
    ._1A(A4), ._1Y(_7405a_2__1y), ._2A(A3), ._2Y(_7405a_2__2y), ._3A(A2), ._3Y(_7405a_2__3y), ._4A(1'b0),
    ._5A(1'b0), ._6A(1'b0), .VCC(1'b1), .GND(1'b0));  // open: _4Y, _5Y, _6Y
  _7430 _7430_1 (
    .pin1(_7405a_2__1y), .pin2(_7405a_2__2y), .pin3(_7405a_2__3y), .pin4(_7430_1_pin4), .pin5(C),
    .pin6(1'b1), .pin7(1'b0), .pin8(_7430_1_pin8), .pin11(1'b1), .pin12(1'b1), .pin14(1'b1));  // open: pin9, pin10, pin13
  _7430 _7430_2 (
    .pin1(_7405a_2__1y), .pin2(_7405a_2__2y), .pin3(A2), .pin4(_7430_1_pin4), .pin5(Z), .pin6(1'b1),
    .pin7(1'b0), .pin8(_7430_2_pin8), .pin11(1'b1), .pin12(1'b1), .pin14(1'b1));  // open: pin9, pin10, pin13
  _7430 _7430_3 (
    .pin1(_7405a_2__1y), .pin2(A3), .pin3(_7405a_2__3y), .pin4(_7430_1_pin4), .pin5(EQ), .pin6(1'b1),
    .pin7(1'b0), .pin8(_7430_3_pin8), .pin11(1'b1), .pin12(1'b1), .pin14(1'b1));  // open: pin9, pin10, pin13
  _7430 _7430_4 (
    .pin1(_7405a_2__1y), .pin2(A3), .pin3(A2), .pin4(_7430_1_pin4), .pin5(NEG), .pin6(1'b1), .pin7(1'b0),
    .pin8(_7430_4_pin8), .pin11(1'b1), .pin12(1'b1), .pin14(1'b1));  // open: pin9, pin10, pin13
  _7430 _7430_5 (
    .pin1(A4), .pin2(_7405a_2__2y), .pin3(_7405a_2__3y), .pin4(_7430_1_pin4), .pin5(OVR), .pin6(1'b1),
    .pin7(1'b0), .pin8(_7430_5_pin8), .pin11(1'b1), .pin12(1'b1), .pin14(1'b1));  // open: pin9, pin10, pin13
  _7421 _7421_1 (
    .pin1(A3), .pin2(A4), .pin4(_7430_1_pin4), .pin5(SWP), .pin6(_7421_1_pin6), .pin7(1'b0),
    .pin8(_7430_1_pin4), .pin9(A5), .pin10(A6), .pin12(A7), .pin13(1'b1), .pin14(1'b1));  // open: pin3, pin11
  Seven_Seg_Hex seven_seg_hex_1 (.d(_7432_2_pin6), .dp(1'b0));
  _7408 _7408_2 (
    .pin1(_7405a_1__2y), .pin2(A7), .pin3(_7408_2_pin3), .pin4(_7405a_1__2y), .pin5(A6), .pin6(_7408_2_pin6),
    .pin7(1'b0), .pin8(_7432_2_pin6[1]), .pin9(_7405a_1__2y), .pin10(A5), .pin11(_7432_2_pin6[0]),
    .pin12(_7405a_1__2y), .pin13(A4), .pin14(1'b1));
  _7408 _7408_3 (
    .pin1(_7405a_1__2y), .pin2(A3), .pin3(_7432_3_pin8[3]), .pin4(_7405a_1__2y), .pin5(A2),
    .pin6(_7432_3_pin8[2]), .pin7(1'b0), .pin8(_7432_3_pin8[1]), .pin9(_7405a_1__2y), .pin10(A1),
    .pin12(_7405a_1__2y), .pin13(1'b0), .pin14(1'b1));  // open: pin11
  _7405A _7405a_3 (
    ._1A(_7430_1_pin8), ._1Y(_7405a_3__1y), ._2A(_7430_2_pin8), ._2Y(_7405a_3__2y), ._3A(_7430_3_pin8),
    ._3Y(_7405a_3__3y), ._4A(_7430_4_pin8), ._4Y(_7405a_3__4y), ._5A(_7430_5_pin8), ._5Y(_7405a_3__5y),
    ._6A(1'b0), .VCC(1'b1), .GND(1'b0));  // open: _6Y
  Seven_Seg_Hex seven_seg_hex_2 (.d(_7432_3_pin8), .dp(1'b0));
  Seven_Seg_Hex seven_seg_hex_3 (.d({A7, A6, A5, A4}), .dp(1'b0));
  Seven_Seg_Hex seven_seg_hex_4 (.d({A3, A2, A1, A0}), .dp(1'b0));
  _7432 _7432_1 (
    .pin1(_7408_1_pin6), .pin2(_7405a_3__1y), .pin3(_7432_1_pin3), .pin4(_7405a_3__2y), .pin5(_7405a_3__3y),
    .pin6(_7432_1_pin6), .pin7(1'b0), .pin8(_7432_1_pin8), .pin9(_7408_1_pin3), .pin10(_7405a_3__4y),
    .pin11(_7432_1_pin11), .pin12(_7405a_3__5y), .pin13(_7421_1_pin6), .pin14(1'b1));
  _7432 _7432_2 (
    .pin1(_7408_2_pin3), .pin2(IRQ), .pin3(_7432_2_pin6[3]), .pin4(_7408_2_pin6), .pin5(IRQ),
    .pin6(_7432_2_pin6[2]), .pin7(1'b0), .pin9(1'b0), .pin10(1'b0), .pin12(1'b0), .pin13(1'b0), .pin14(1'b1));  // open: pin8, pin11
  _7432 _7432_3 (
    .pin1(_7432_1_pin6), .pin2(_7432_1_pin3), .pin3(_7432_3_pin3), .pin4(_7432_1_pin11), .pin5(_7432_1_pin8),
    .pin6(_7432_3_pin6), .pin7(1'b0), .pin8(_7432_3_pin8[0]), .pin9(_7432_3_pin6), .pin10(_7432_3_pin3),
    .pin12(1'b0), .pin13(1'b0), .pin14(1'b1));  // open: pin11
  _28c16_Decode4 _28c16_decode4_1 (
    .A0(_7432_3_pin8[0]), .A1(_7432_3_pin8[1]), .A2(_7432_3_pin8[2]), .A3(_7432_3_pin8[3]),
    .A4(_7432_2_pin6[0]), .A5(_7432_2_pin6[1]), .A6(_7432_2_pin6[2]), .A7(_7432_2_pin6[3]), .A8(1'b0),
    .A9(1'b0), .A10(1'b0), .nCE(1'b0), .nOE(1'b0), .nWE(1'b1), .VCC(1'b1), .GND(1'b0), .I_O0(IV_EIN),
    .I_O1(IV_EOUT), .I_O2(IRQ_ON), .I_O3(IRQ_OFF), .I_O4(IRQ_SUP_ON), .I_O5(IRQ_SUP_OFF), .I_O6(INC),
    .I_O7(HALT));
  _28c16_Decode3 _28c16_decode3_1 (
    .A0(_7432_3_pin8[0]), .A1(_7432_3_pin8[1]), .A2(_7432_3_pin8[2]), .A3(_7432_3_pin8[3]),
    .A4(_7432_2_pin6[0]), .A5(_7432_2_pin6[1]), .A6(_7432_2_pin6[2]), .A7(_7432_2_pin6[3]), .A8(1'b0),
    .A9(1'b0), .A10(1'b0), .nCE(1'b0), .nOE(1'b0), .nWE(1'b1), .VCC(1'b1), .GND(1'b0), .I_O0(S0), .I_O1(S1),
    .I_O2(S2), .I_O3(S3), .I_O4(P0), .I_O5(P1), .I_O6(P2), .I_O7(PG));
  _28c16_Decode2 _28c16_decode2_1 (
    .A0(_7432_3_pin8[0]), .A1(_7432_3_pin8[1]), .A2(_7432_3_pin8[2]), .A3(_7432_3_pin8[3]),
    .A4(_7432_2_pin6[0]), .A5(_7432_2_pin6[1]), .A6(_7432_2_pin6[2]), .A7(_7432_2_pin6[3]), .A8(1'b0),
    .A9(1'b0), .A10(1'b0), .nCE(_7405a_1__1y), .nOE(1'b0), .nWE(1'b1), .VCC(1'b1), .GND(1'b0),
    .I_O0(MEM_EIN), .I_O1(MEM_EOUT), .I_O2(MEMAL_EIN), .I_O3(MEMAH_EIN), .I_O4(STK_EOUT), .I_O5(ROM_EAOUT),
    .I_O6(PC_EOUT), .I_O7(RST));
  _28c16_Decode1 _28c16_decode1_1 (
    .A0(_7432_3_pin8[0]), .A1(_7432_3_pin8[1]), .A2(_7432_3_pin8[2]), .A3(_7432_3_pin8[3]),
    .A4(_7432_2_pin6[0]), .A5(_7432_2_pin6[1]), .A6(_7432_2_pin6[2]), .A7(_7432_2_pin6[3]), .A8(1'b0),
    .A9(1'b0), .A10(1'b0), .nCE(_7405a_1__1y), .nOE(1'b0), .nWE(1'b1), .VCC(1'b1), .GND(1'b0),
    .I_O0(REGS2_EIN), .I_O1(REGS2_EOUT), .I_O2(REGF1_EIN), .I_O3(REGF1_EOUT), .I_O4(REGF2_EIN),
    .I_O5(REGF2_EOUT), .I_O6(PC_EIN), .I_O7(ROM_EDOUT));
  _28c16_Decode0 _28c16_decode0_1 (
    .A0(_7432_3_pin8[0]), .A1(_7432_3_pin8[1]), .A2(_7432_3_pin8[2]), .A3(_7432_3_pin8[3]),
    .A4(_7432_2_pin6[0]), .A5(_7432_2_pin6[1]), .A6(_7432_2_pin6[2]), .A7(_7432_2_pin6[3]), .A8(1'b0),
    .A9(1'b0), .A10(1'b0), .nCE(_7405a_1__1y), .nOE(1'b0), .nWE(1'b1), .VCC(1'b1), .GND(1'b0),
    .I_O0(REGA_EIN), .I_O1(REGA_EOUT), .I_O2(REGB_EIN), .I_O3(REGB_EOUT), .I_O4(REGC_EIN), .I_O5(REGC_EOUT),
    .I_O6(REGS1_EIN), .I_O7(REGS1_EOUT));
  PullDown pulldown_1 (.out(HALT));
  PullDown pulldown_2 (.out(PG));
  PullDown pulldown_3 (.out(RST));
  PullDown pulldown_4 (.out(ROM_EDOUT));
  PullDown pulldown_5 (.out(REGS1_EOUT));
  PullDown pulldown_6 (.out(IRQ_SUP_OFF));
  PullDown pulldown_7 (.out(INC));
  PullDown pulldown_8 (.out(P1));
  PullDown pulldown_9 (.out(P2));
  PullDown pulldown_10 (.out(PC_EOUT));
  PullDown pulldown_11 (.out(ROM_EAOUT));
  PullDown pulldown_12 (.out(PC_EIN));
  PullDown pulldown_13 (.out(REGF2_EOUT));
  PullDown pulldown_14 (.out(REGS1_EIN));
  PullDown pulldown_15 (.out(REGC_EOUT));
  PullDown pulldown_16 (.out(IRQ_SUP_ON));
  PullDown pulldown_17 (.out(IRQ_OFF));
  PullDown pulldown_18 (.out(P0));
  PullDown pulldown_19 (.out(S3));
  PullDown pulldown_20 (.out(STK_EOUT));
  PullDown pulldown_21 (.out(MEMAH_EIN));
  PullDown pulldown_22 (.out(REGF2_EIN));
  PullDown pulldown_23 (.out(REGF1_EOUT));
  PullDown pulldown_24 (.out(REGC_EIN));
  PullDown pulldown_25 (.out(REGB_EOUT));
  PullDown pulldown_26 (.out(IRQ_ON));
  PullDown pulldown_27 (.out(IV_EOUT));
  PullDown pulldown_28 (.out(S2));
  PullDown pulldown_29 (.out(S1));
  PullDown pulldown_30 (.out(MEMAL_EIN));
  PullDown pulldown_31 (.out(MEM_EOUT));
  PullDown pulldown_32 (.out(REGF1_EIN));
  PullDown pulldown_33 (.out(REGS2_EOUT));
  PullDown pulldown_34 (.out(REGB_EIN));
  PullDown pulldown_35 (.out(REGA_EOUT));
  PullDown pulldown_36 (.out(IV_EIN));
  PullDown pulldown_37 (.out(S0));
  PullDown pulldown_38 (.out(MEM_EIN));
  PullDown pulldown_39 (.out(REGS2_EIN));
  PullDown pulldown_40 (.out(REGA_EIN));

  // Notes on the sheet:
  //   A7: pin 1
  //   A6: pin 2
  //   A5: pin 3
  //   A4: pin 4
  //   A3: pin 5
  //   A2: pin 6
  //   A1: pin 7
  //   A0: pin 8
  //   ROM_EDOUT: pin 47
  //   PC_EIN: pin 46
  //   REGF2_EOUT: pin 45
  //   REGF2_EIN: pin 44
  //   REGF1_EOUT: pin 43
  //   REGF1_EIN: pin 42
  //   REGS2_EOUT: pin 41
  //   REGS2_EIN: pin 20
  //   PC_EOUT: pin 54
  //   ROM_EAOUT: pin 53
  //   STK_EOUT: pin 52
  //   MEMAH_EIN: pin 51
  //   MEMAL_EIN: pin 50
  //   MEM_EOUT: pin 49
  //   MEM_EIN: pin 48
  //   REGS1_EOUT: pin 19
  //   REGS1_EIN: pin 18
  //   REGC_EOUT: pin 17
  //   REGC_EIN: pin 16
  //   REGB_EOUT: pin 15
  //   REGB_EIN: pin 14
  //   REGA_EOUT: pin 13
  //   REGA_EIN: pin 12
  //   C: pin 9
  //   Z: pin 10
  //   EQ: pin 11
  //   SWP: pin 35
  //   S0: pin 57
  //   S1: pin 58
  //   S2: pin 59
  //   RST: pin 56
  //   ENABLE: pin 55
  //   P0: pin 21
  //   P1: pin 22
  //   P2: pin 23
  //   PG: pin 24
  //   INC: pin 37
  //   IV_EIN: pin 25
  //   IV_EOUT: pin 26
  //   IRQ_ON: pin 27
  //   IRQ_OFF: pin 28
  //   IRQ_SUP_ON: pin 33
  //   IRQ_SUP_OFF: pin 34
  //   S3: pin 60
  //   HALT: pin 36
  //   SPARE4: pin 38
  //   NEG: pin 39
  //   OVR: pin 40
  //   IRQ: pin 29
  //   SPARE1: pin 30
  //   SPARE2: pin 31
  //   SPARE3: pin 32
  //   Temp output to view on main board
  //   BCS/BCC - 000
  //   BZS/BZC - 001
  //   BES/BEC - 010
  //   BNS/BNC - 011
  //   BOS/BOC - 100
  //   SWP
  //   Actual Instruction
  //   Instruction
endmodule

/* Test case Check Decoding - Standard 0-15:
A7 A6 A5 A4 A3 A2 A1 A0 C Z EQ NEG OVR SWP IRQ ENABLE REGA-EIN REGA-EOUT REGB-EIN REGB-EOUT REGC-EIN REGC-EOUT REGS1-EIN REGS1-EOUT REGS2-EIN REGS2-EOUT REGF1-EIN REGF1-EOUT REGF2-EIN REGF2-EOUT PC-EIN ROM-EDOUT MEM-EIN MEM-EOUT MEMAL-EIN MEMAH-EIN STK-EOUT ROM-EAOUT PC-EOUT RST S3 S2 S1 S0 P2 P1 P0 PG IV-EIN IV-EOUT SPARE1 SPARE2 SPARE3 SPARE4 INC HALT
#   0 - NULL
0  0  0  0  0  0  0  0  0 0 0  0   0   0   0   1      0        0         0        0         0        0         0         0          0          0         0         0          0         0          0      0         0       0        0         0         0        0         0       0   0  0  0  0  0  0  0  0  0      0       0      0      0      0      0   0
#   1 - MOV R M 
0  0  0  0  0  0  0  1  0 0 0  0   0   0   0   1      0        0         0        0         0        0         0         0          0          0         0         0          0         0          0      1         1       0        0         0         0        0         0       0   0  0  0  1  0  0  0  0  0      0       0      0      0      0      0   0
#   2 - MOV R MAL
0  0  0  0  0  0  1  0  0 0 0  0   0   0   0   1      0        0         0        0         0        0         0         0          0          0         0         0          0         0          0      1         0       0        1         0         0        0         0       0   0  0  0  1  0  0  0  0  0      0       0      0      0      0      0   0
#   3 - MOV R MAH
0  0  0  0  0  0  1  1  0 0 0  0   0   0   0   1      0        0         0        0         0        0         0         0          0          0         0         0          0         0          0      1         0       0        0         1         0        0         0       0   0  0  0  1  0  0  0  0  0      0       0      0      0      0      0   0
#   4 - MOV R A
0  0  0  0  0  1  0  0  0 0 0  0   0   0   0   1      1        0         0        0         0        0         0         0          0          0         0         0          0         0          0      1         0       0        0         0         0        0         0       0   0  0  0  1  0  0  0  0  0      0       0      0      0      0      0   0
#   5 - MOV R B
0  0  0  0  0  1  0  1  0 0 0  0   0   0   0   1      0        0         1        0         0        0         0         0          0          0         0         0          0         0          0      1         0       0        0         0         0        0         0       0   0  0  0  1  0  0  0  0  0      0       0      0      0      0      0   0
#   6 - MOV R S1
0  0  0  0  0  1  1  0  0 0 0  0   0   0   0   1      0        0         0        0         0        0         1         0          0          0         0         0          0         0          0      1         0       0        0         0         0        0         0       0   0  0  0  1  0  0  0  0  0      0       0      0      0      0      0   0
#   7 - MOV R S2
0  0  0  0  0  1  1  1  0 0 0  0   0   0   0   1      0        0         0        0         0        0         0         0          1          0         0         0          0         0          0      1         0       0        0         0         0        0         0       0   0  0  0  1  0  0  0  0  0      0       0      0      0      0      0   0
#   8 - MOV R IV
0  0  0  0  1  0  0  0  0 0 0  0   0   0   0   1      0        0         0        0         0        0         0         0          0          0         0         0          0         0          0      1         0       0        0         0         0        0         0       0   0  0  0  1  0  0  0  0  1      0       0      0      0      0      0   0
#   9 - UNUSED
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*/

/* Test case Check Decoding Standard 16-31:
A7 A6 A5 A4 A3 A2 A1 A0 C Z EQ NEG OVR SWP IRQ ENABLE REGA-EIN REGA-EOUT REGB-EIN REGB-EOUT REGC-EIN REGC-EOUT REGS1-EIN REGS1-EOUT REGS2-EIN REGS2-EOUT REGF1-EIN REGF1-EOUT REGF2-EIN REGF2-EOUT PC-EIN ROM-EDOUT MEM-EIN MEM-EOUT MEMAL-EIN MEMAH-EIN STK-EOUT ROM-EAOUT PC-EOUT RST S3 S2 S1 S0 P2 P1 P0 PG IV-EIN IV-EOUT SPARE1 SPARE2 SPARE3 SPARE4 INC HALT
#  16 - MOV M PC
0  0  0  1  0  0  0  0  0 0 0  0   0   0   0   1      0        0         0        0         0        0         0         0          0         0          0         0          0         0          1      0         0       1        0         0         0        0         0       0   0  1  1  0  0  0  0  0  0      0       0      0      0      0      0   0
#  17 - MOV M A
0  0  0  1  0  0  0  1  0 0 0  0   0   0   0   1      1        0         0        0         0        0         0         0          0         0          0         0          0         0          0      0         0       1        0         0         0        0         0       0   0  0  0  1  0  0  0  0  0      0       0      0      0      0      0   0
#  18 - MOV M B
0  0  0  1  0  0  1  0  0 0 0  0   0   0   0   1      0        0         1        0         0        0         0         0          0         0          0         0          0         0          0      0         0       1        0         0         0        0         0       0   0  0  0  1  0  0  0  0  0      0       0      0      0      0      0   0
#  19 - MOV M S1
0  0  0  1  0  0  1  1  0 0 0  0   0   0   0   1      0        0         0        0         0        0         1         0          0         0          0         0          0         0          0      0         0       1        0         0         0        0         0       0   0  0  0  1  0  0  0  0  0      0       0      0      0      0      0   0
#  20 - MOV M S2
0  0  0  1  0  1  0  0  0 0 0  0   0   0   0   1      0        0         0        0         0        0         0         0          1         0          0         0          0         0          0      0         0       1        0         0         0        0         0       0   0  0  0  1  0  0  0  0  0      0       0      0      0      0      0   0
#  21 - MOV M IV
0  0  0  1  0  1  0  1  0 0 0  0   0   0   0   1      0        0         0        0         0        0         0         0          0         0          0         0          0         0          0      0         0       1        0         0         0        0         0       0   0  0  0  1  0  0  0  0  1      0       0      0      0      0      0   0
#  22 - UNUSED
0  0  0  1  0  1  1  0  0 0 0  0   0   0   0   1      0        0         0        0         0        0         0         0          0          0         0         0          0         0          0      0         0       0        0         0         0        0         0       0   0  0  0  0  0  0  0  0  0      0       0      0      0      0      0   0
#  23 - UNUSED
0  0  0  1  0  1  1  1  0 0 0  0   0   0   0   1      0        0         0        0         0        0         0         0          0          0         0         0          0         0          0      0         0       0        0         0         0        0         0       0   0  0  0  0  0  0  0  0  0      0       0      0      0      0      0   0
#  24 - UNUSED
0  0  0  1  1  0  0  0  0 0 0  0   0   0   0   1      0        0         0        0         0        0         0         0          0          0         0         0          0         0          0      0         0       0        0         0         0        0         0       0   0  0  0  0  0  0  0  0  0      0       0      0      0      0      0   0
#  25 - UNUSED
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*/

/* Test case Check Decoding - Standard 32-47:
A7 A6 A5 A4 A3 A2 A1 A0 C Z EQ NEG OVR SWP IRQ ENABLE REGA-EIN REGA-EOUT REGB-EIN REGB-EOUT REGC-EIN REGC-EOUT REGS1-EIN REGS1-EOUT REGS2-EIN REGS2-EOUT REGF1-EIN REGF1-EOUT REGF2-EIN REGF2-EOUT PC-EIN ROM-EDOUT MEM-EIN MEM-EOUT MEMAL-EIN MEMAH-EIN STK-EOUT ROM-EAOUT PC-EOUT RST S3 S2 S1 S0 P2 P1 P0 PG IV-EIN IV-EOUT SPARE1 SPARE2 SPARE3 SPARE4 INC HALT
#  32 - INC A
0  0  1  0  0  0  0  0  0 0 0  0   0   0   0   1      1        0         0        0         0        0         0         0          0         0          0         0          0         0          0      0         0       0        0         0         0        0         0       0   0  0  0  0  0  0  0  0  0      0       0      0      0      0      1   0
#  33 - INC B
0  0  1  0  0  0  0  1  0 0 0  0   0   0   0   1      0        0         1        0         0        0         0         0          0         0          0         0          0         0          0      0         0       0        0         0         0        0         0       0   0  0  0  0  0  0  0  0  0      0       0      0      0      0      1   0
#  34 - INC C
0  0  1  0  0  0  1  0  0 0 0  0   0   0   0   1      0        0         0        0         1        0         0         0          0         0          0         0          0         0          0      0         0       0        0         0         0        0         0       0   0  0  0  0  0  0  0  0  0      0       0      0      0      0      1   0
#  35 - INC MA
0  0  1  0  0  0  1  1  0 0 0  0   0   0   0   1      0        0         0        0         0        0         0         0          0         0          0         0          0         0          0      0         0       0        1         0         0        0         0       0   0  0  0  0  0  0  0  0  0      0       0      0      0      0      1   0
#  36 - UNUSED
0  0  1  0  0  1  0  0  0 0 0  0   0   0   0   1      0        0         0        0         0        0         0         0          0          0         0         0          0         0          0      0         0       0        0         0         0        0         0       0   0  0  0  0  0  0  0  0  0      0       0      0      0      0      0   0
#  37 - UNUSED
0  0  1  0  0  1  0  1  0 0 0  0   0   0   0   1      0        0         0        0         0        0         0         0          0          0         0         0          0         0          0      0         0       0        0         0         0        0         0       0   0  0  0  0  0  0  0  0  0      0       0      0      0      0      0   0
#  38 - UNUSED
0  0  1  0  0  1  1  0  0 0 0  0   0   0   0   1      0        0         0        0         0        0         0         0          0          0         0         0          0         0          0      0         0       0        0         0         0        0         0       0   0  0  0  0  0  0  0  0  0      0       0      0      0      0      0   0
#  39 - UNUSED
0  0  1  0  0  1  1  1  0 0 0  0   0   0   0   1      0        0         0        0         0        0         0         0          0          0         0         0          0         0          0      0         0       0        0         0         0        0         0       0   0  0  0  0  0  0  0  0  0      0       0      0      0      0      0   0
#  40 - UNUSED
0  0  1  0  1  0  0  0  0 0 0  0   0   0   0   1      0        0         0        0         0        0         0         0          0          0         0         0          0         0          0      0         0       0        0         0         0        0         0       0   0  0  0  0  0  0  0  0  0      0       0      0      0      0      0   0
#  41 - UNUSED
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*/

/* Test case Check Decoding - Standard 48-63:
A7 A6 A5 A4 A3 A2 A1 A0 C Z EQ NEG OVR SWP IRQ ENABLE REGA-EIN REGA-EOUT REGB-EIN REGB-EOUT REGC-EIN REGC-EOUT REGS1-EIN REGS1-EOUT REGS2-EIN REGS2-EOUT REGF1-EIN REGF1-EOUT REGF2-EIN REGF2-EOUT PC-EIN ROM-EDOUT MEM-EIN MEM-EOUT MEMAL-EIN MEMAH-EIN STK-EOUT ROM-EAOUT PC-EOUT RST S3 S2 S1 S0 P2 P1 P0 PG IV-EIN IV-EOUT SPARE1 SPARE2 SPARE3 SPARE4 INC HALT
#  48 - MOV A PC
0  0  1  1  0  0  0  0  0 0 0  0   0   0   0   1      0        1         0        0         0        0         0         0          0         0          0         0          0         0          1      0         0       0        0         0         0        0         0       0   0  1  1  0  0  0  0  0  0      0       0      0      0      0      0   0
#  49 - MOV A MEM
0  0  1  1  0  0  0  1  0 0 0  0   0   0   0   1      0        1         0        0         0        0         0         0          0         0          0         0          0         0          0      0         1       0        0         0         0        0         0       0   0  0  0  1  0  0  0  0  0      0       0      0      0      0      0   0
#  50 - MOV A MEMAL
0  0  1  1  0  0  1  0  0 0 0  0   0   0   0   1      0        1         0        0         0        0         0         0          0         0          0         0          0         0          0      0         0       0        1         0         0        0         0       0   0  0  0  1  0  0  0  0  0      0       0      0      0      0      0   0
#  51 - MOV A MEMAH
0  0  1  1  0  0  1  1  0 0 0  0   0   0   0   1      0        1         0        0         0        0         0         0          0         0          0         0          0         0          0      0         0       0        0         1         0        0         0       0   0  0  0  1  0  0  0  0  0      0       0      0      0      0      0   0
#  52 - MOV A B
0  0  1  1  0  1  0  0  0 0 0  0   0   0   0   1      0        1         1        0         0        0         0         0          0         0          0         0          0         0          0      0         0       0        0         0         0        0         0       0   0  0  0  1  0  0  0  0  0      0       0      0      0      0      0   0
#  53 - MOV A S1
0  0  1  1  0  1  0  1  0 0 0  0   0   0   0   1      0        1         0        0         0        0         1         0          0         0          0         0          0         0          0      0         0       0        0         0         0        0         0       0   0  0  0  1  0  0  0  0  0      0       0      0      0      0      0   0
#  54 - MOV A S2
0  0  1  1  0  1  1  0  0 0 0  0   0   0   0   1      0        1         0        0         0        0         0         0          1         0          0         0          0         0          0      0         0       0        0         0         0        0         0       0   0  0  0  1  0  0  0  0  0      0       0      0      0      0      0   0
#  55 - MOV A IV
0  0  1  1  0  1  1  1  0 0 0  0   0   0   0   1      0        0         0        0         0        0         0         0          0         0          0         0          0         0          0      0         0       0        0         0         0        0         0       0   0  0  0  1  0  0  0  0  0      0       0      0      0      0      0   0
#  56 - UNUSED
0  0  1  1  1  0  0  0  0 0 0  0   0   0   0   1      0        0         0        0         0        0         0         0          0          0         0         0          0         0          0      0         0       0        0         0         0        0         0       0   0  0  0  0  0  0  0  0  0      0       0      0      0      0      0   0
#  57 - UNUSED
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*/

/* Test case Check Decoding - Standar 64-79:
###############
A7 A6 A5 A4 A3 A2 A1 A0 C Z EQ NEG OVR SWP IRQ ENABLE REGA-EIN REGA-EOUT REGB-EIN REGB-EOUT REGC-EIN REGC-EOUT REGS1-EIN REGS1-EOUT REGS2-EIN REGS2-EOUT REGF1-EIN REGF1-EOUT REGF2-EIN REGF2-EOUT PC-EIN ROM-EDOUT MEM-EIN MEM-EOUT MEMAL-EIN MEMAH-EIN STK-EOUT ROM-EAOUT PC-EOUT RST S3 S2 S1 S0 P2 P1 P0 PG IV-EIN IV-EOUT SPARE1 SPARE2 SPARE3 SPARE4 INC HALT
#  64 - MOV B PC
0  1  0  0  0  0  0  0  0 0 0  0  0    0   0   1      0        0         0        1         0        0         0         0          0         0          0         0          0         0          1      0         0       0        0         0         0        0         0       0   0  1  1  0  0  0  0  0  0      0       0      0      0      0      0   0
#  65 - MOV B MEM
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*/

/* Test case Check Decoding - Standard 80-95:
A7 A6 A5 A4 A3 A2 A1 A0 C Z EQ NEG OVR SWP IRQ ENABLE REGA-EIN REGA-EOUT REGB-EIN REGB-EOUT REGC-EIN REGC-EOUT REGS1-EIN REGS1-EOUT REGS2-EIN REGS2-EOUT REGF1-EIN REGF1-EOUT REGF2-EIN REGF2-EOUT PC-EIN ROM-EDOUT MEM-EIN MEM-EOUT MEMAL-EIN MEMAH-EIN STK-EOUT ROM-EAOUT PC-EOUT RST S3 S2 S1 S0 P2 P1 P0
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*/

/* Test case Check Decoding - Standard 96-127:
A7 A6 A5 A4 A3 A2 A1 A0 C Z EQ NEG OVR SWP IRQ ENABLE REGA-EIN REGA-EOUT REGB-EIN REGB-EOUT REGC-EIN REGC-EOUT REGS1-EIN REGS1-EOUT REGS2-EIN REGS2-EOUT REGF1-EIN REGF1-EOUT REGF2-EIN REGF2-EOUT PC-EIN ROM-EDOUT MEM-EIN MEM-EOUT MEMAL-EIN MEMAH-EIN STK-EOUT ROM-EAOUT PC-EOUT RST S3 S2 S1 S0 P2 P1 P0
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*/

/* Test case Check Decoding - Standard 144-159:
A7 A6 A5 A4 A3 A2 A1 A0 C Z EQ NEG OVR SWP IRQ ENABLE REGA-EIN REGA-EOUT REGB-EIN REGB-EOUT REGC-EIN REGC-EOUT REGS1-EIN REGS1-EOUT REGS2-EIN REGS2-EOUT REGF1-EIN REGF1-EOUT REGF2-EIN REGF2-EOUT PC-EIN ROM-EDOUT MEM-EIN MEM-EOUT MEMAL-EIN MEMAH-EIN STK-EOUT ROM-EAOUT PC-EOUT RST S3 S2 S1 S0 P2 P1 P0
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*/

/* Test case Check Decoding - Standard 199-223:
A7 A6 A5 A4 A3 A2 A1 A0 C Z EQ NEG OVR SWP IRQ ENABLE REGA-EIN REGA-EOUT REGB-EIN REGB-EOUT REGC-EIN REGC-EOUT REGS1-EIN REGS1-EOUT REGS2-EIN REGS2-EOUT REGF1-EIN REGF1-EOUT REGF2-EIN REGF2-EOUT PC-EIN ROM-EDOUT MEM-EIN MEM-EOUT MEMAL-EIN MEMAH-EIN STK-EOUT ROM-EAOUT PC-EOUT RST S3 S2 S1 S0 P2 P1 P0
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*/

/* Test case Check Decoding - BCS:
A7 A6 A5 A4 A3 A2 A1 A0 C Z EQ NEG OVR SWP IRQ ENABLE REGA-EIN REGA-EOUT REGB-EIN REGB-EOUT REGC-EIN REGC-EOUT REGS1-EIN REGS1-EOUT REGS2-EIN REGS2-EOUT REGF1-EIN REGF1-EOUT REGF2-EIN REGF2-EOUT PC-EIN ROM-EDOUT MEM-EIN MEM-EOUT MEMAL-EIN MEMAH-EIN STK-EOUT ROM-EAOUT PC-EOUT RST S3 S2 S1 S0 P2 P1 P0
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*/

/* Test case Check Decoding - Branches:
A7 A6 A5 A4 A3 A2 A1 A0 C Z EQ NEG OVR SWP IRQ ENABLE REGA-EIN REGA-EOUT REGB-EIN REGB-EOUT REGC-EIN REGC-EOUT REGS1-EIN REGS1-EOUT REGS2-EIN REGS2-EOUT REGF1-EIN REGF1-EOUT REGF2-EIN REGF2-EOUT PC-EIN ROM-EDOUT MEM-EIN MEM-EOUT MEMAL-EIN MEMAH-EIN STK-EOUT ROM-EAOUT PC-EOUT RST S3 S2 S1 S0 P2 P1 P0
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*/

/* Test case CheckDecoding - Jump Sub:
A7 A6 A5 A4 A3 A2 A1 A0 C Z EQ NEG OVR SWP IRQ ENABLE REGA-EIN REGA-EOUT REGB-EIN REGB-EOUT REGC-EIN REGC-EOUT REGS1-EIN REGS1-EOUT REGS2-EIN REGS2-EOUT REGF1-EIN REGF1-EOUT REGF2-EIN REGF2-EOUT PC-EIN ROM-EDOUT MEM-EIN MEM-EOUT MEMAL-EIN MEMAH-EIN STK-EOUT ROM-EAOUT PC-EOUT RST S3 S2 S1 S0 P2 P1 P0
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*/

/* Test case Check Decoding - PUSH & POP:
A7 A6 A5 A4 A3 A2 A1 A0 C Z EQ NEG OVR SWP IRQ ENABLE REGA-EIN REGA-EOUT REGB-EIN REGB-EOUT REGC-EIN REGC-EOUT REGS1-EIN REGS1-EOUT REGS2-EIN REGS2-EOUT REGF1-EIN REGF1-EOUT REGF2-EIN REGF2-EOUT PC-EIN ROM-EDOUT MEM-EIN MEM-EOUT MEMAL-EIN MEMAH-EIN STK-EOUT ROM-EAOUT PC-EOUT RST S3 S2 S1 S0 P2 P1 P0
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*/

/* Test case Check Decoding - EXE & RST:
A7 A6 A5 A4 A3 A2 A1 A0 C Z EQ NEG OVR SWP IRQ ENABLE REGA-EIN REGA-EOUT REGB-EIN REGB-EOUT REGC-EIN REGC-EOUT REGS1-EIN REGS1-EOUT REGS2-EIN REGS2-EOUT REGF1-EIN REGF1-EOUT REGF2-EIN REGF2-EOUT PC-EIN ROM-EDOUT MEM-EIN MEM-EOUT MEMAL-EIN MEMAH-EIN STK-EOUT ROM-EAOUT PC-EOUT RST S3 S2 S1 S0 P2 P1 P0
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*/

/* Test case Check Decoding - Interrupts:
A7 A6 A5 A4 A3 A2 A1 A0 C Z EQ NEG OVR SWP IRQ ENABLE REGA-EIN REGA-EOUT REGB-EIN REGB-EOUT REGC-EIN REGC-EOUT REGS1-EIN REGS1-EOUT REGS2-EIN REGS2-EOUT REGF1-EIN REGF1-EOUT REGF2-EIN REGF2-EOUT PC-EIN ROM-EDOUT MEM-EIN MEM-EOUT MEMAL-EIN MEMAH-EIN STK-EOUT ROM-EAOUT PC-EOUT RST S3 S2 S1 S0 P2 P1 P0
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*/
