// Digital circuit FLAGS.dig as structural Verilog
module FLAGS (
  input  D3,
  input  D2,
  input  D1,
  input  D0,
  input  REG_SET,
  input  REG_OUT,
  input  REG_IN,
  input  REG_CLR,
  input  CIN_SET,
  input  CIN_VAL,
  output M0,
  output M1,
  output M2,
  output M3
);

  wire _7404_1_pin2, _7404_1_pin4, _7404_1_pin6, _74157_1_pin4, _74157_1_pin7, _74157_1_pin9, _74157_1_pin12;

  _7404 _7404_1 (
    .pin1(REG_IN), .pin2(_7404_1_pin2), .pin3(REG_CLR), .pin4(_7404_1_pin4), .pin5(REG_OUT),
    .pin6(_7404_1_pin6), .pin7(1'b0), .pin9(1'b0), .pin11(1'b0), .pin13(1'b0), .pin14(1'b1));  // open: pin8, pin10, pin12
  _74157 _74157_1 (
    .pin1(CIN_SET), .pin2(D0), .pin3(CIN_VAL), .pin4(_74157_1_pin4), .pin5(D1), .pin6(M1),
    .pin7(_74157_1_pin7), .pin8(1'b0), .pin9(_74157_1_pin9), .pin10(M2), .pin11(D2), .pin12(_74157_1_pin12),
    .pin13(M3), .pin14(D3), .pin15(1'b0), .pin16(1'b1));
  _74161 _74161_1 (
    .pin1(_7404_1_pin4), .pin2(REG_SET), .pin3(_74157_1_pin4), .pin4(_74157_1_pin7), .pin5(_74157_1_pin9),
    .pin6(_74157_1_pin12), .pin7(1'b0), .pin8(1'b0), .pin9(_7404_1_pin2), .pin10(1'b0), .pin11(M3),
    .pin12(M2), .pin13(M1), .pin14(M0), .pin16(1'b1));  // open: pin15
  _74244 _74244_1 (
    .pin1(_7404_1_pin6), .pin2(1'b0), .pin3(D0), .pin4(1'b0), .pin5(D1), .pin6(1'b0), .pin7(D2), .pin8(1'b0),
    .pin9(D3), .pin10(1'b0), .pin11(M3), .pin13(M2), .pin15(M1), .pin17(M0), .pin19(_7404_1_pin6),
    .pin20(1'b1));  // open: pin12, pin14, pin16, pin18
endmodule
