// Digital circuit INT.dig as structural Verilog
module INT (
  input  clk
);

  wire and_1_out, and_2_out, and_3_out, d_ff_1_nq, d_ff_1_q, d_ff_2_q, or_1_out, rs_ff_as_1_q, rs_ff_as_2_q,
       rs_ff_as_3_q, rs_ff_as_4_nq, rs_ff_as_4_q, switch_1_b, undriven, undriven_2;

  Switch switch_1 (.A(1'b1), .B(switch_1_b));
  PullDown pulldown_1 (.out(switch_1_b));
  D_FF d_ff_1 (.D(switch_1_b), .C(clk), .Q(d_ff_1_q), .nQ(d_ff_1_nq));
  D_FF d_ff_2 (.D(d_ff_1_nq), .C(clk), .Q(d_ff_2_q));  // open: nQ
  and and_1 (and_1_out, d_ff_1_q, d_ff_2_q);
  or or_1 (or_1_out, clk, rs_ff_as_1_q);
  LED led_1 (.in(and_1_out));
  RS_FF_AS rs_ff_as_1 (.S(and_1_out), .R(undriven), .Q(rs_ff_as_1_q));  // open: nQ
  RS_FF_AS rs_ff_as_2 (.S(or_1_out), .R(undriven), .Q(rs_ff_as_2_q));  // open: nQ
  and and_2 (and_2_out, clk, rs_ff_as_2_q);
  and and_3 (and_3_out, and_2_out, rs_ff_as_4_nq);
  RS_FF_AS rs_ff_as_3 (.S(and_3_out), .R(undriven), .Q(rs_ff_as_3_q));  // open: nQ
  RS_FF_AS rs_ff_as_4 (.S(and_3_out), .R(undriven_2), .Q(rs_ff_as_4_q), .nQ(rs_ff_as_4_nq));
  LED INT (.in(rs_ff_as_3_q));
  LED INTSUP (.in(rs_ff_as_4_q));
endmodule
