// Digital circuit IRQ.dig as structural Verilog
module IRQ (
  input  IRQ_CLR,
  input  IRQSUP_CLR,
  input  IRQ_IN,
  input  IRQ_MAN,
  input  IRQSUP_SET,
  input  clk,
  output IRQ,
  output RESET
);

  wire _7404_1_pin4, _7404_1_pin5, _7404_1_pin6, _7404_1_pin9, _7404_1_pin12, _7474_1_pin3, _7474_1_pin5,
       _7474_1_pin8, _7474_2_pin2, _74161_1_pin7, _74161_1_pin14, _74161_2_pin11, _74161_2_pin12,
       _74161_2_pin13, _74161_2_pin14, CLK_CLR_out, nor_1_out, nor_2_out, nor_3_out, or_1_out;

  PullDown pulldown_1 (.out(IRQ_MAN));
  or or_1 (or_1_out, IRQ_IN, IRQ_MAN);
  Button u_RESET (.out(RESET));
  Button CLK_CLR (.out(CLK_CLR_out));
  nor nor_1 (nor_1_out, IRQSUP_SET, RESET);
  _7474 _7474_1 (
    .pin1(1'b1), .pin2(or_1_out), .pin3(_7474_1_pin3), .pin4(1'b1), .pin5(_7474_1_pin5), .pin7(1'b0),
    .pin8(_7474_1_pin8), .pin9(_7474_1_pin3), .pin10(1'b1), .pin11(clk), .pin12(_7474_1_pin8), .pin13(1'b1),
    .pin14(1'b1));  // open: pin6
  nor nor_2 (nor_2_out, IRQ_CLR, RESET);
  nor nor_3 (nor_3_out, _7404_1_pin9, CLK_CLR_out, RESET);
  _7404 _7404_1 (
    .pin1(1'b0), .pin3(_7474_1_pin5), .pin4(_7404_1_pin4), .pin5(_7404_1_pin5), .pin6(_7404_1_pin6),
    .pin7(1'b0), .pin9(_7404_1_pin9), .pin11(1'b0), .pin12(_7404_1_pin12), .pin13(IRQSUP_CLR), .pin14(1'b1));  // open: pin2, pin8, pin10
  _7474 _7474_2 (
    .pin1(nor_2_out), .pin2(_7474_2_pin2), .pin3(_7474_1_pin3), .pin4(_7404_1_pin4), .pin5(_7474_2_pin2),
    .pin7(1'b0), .pin9(_7404_1_pin5), .pin10(nor_1_out), .pin11(_7474_1_pin3), .pin12(_7404_1_pin5),
    .pin13(_7404_1_pin12), .pin14(1'b1));  // open: pin6, pin8
  _74161 _74161_1 (
    .pin1(nor_3_out), .pin2(_7474_1_pin3), .pin3(1'b0), .pin4(1'b0), .pin5(1'b0), .pin6(1'b0),
    .pin7(_74161_1_pin7), .pin8(1'b0), .pin9(1'b1), .pin10(_74161_1_pin7), .pin13(_7404_1_pin9),
    .pin14(_74161_1_pin14), .pin16(1'b1));  // open: pin11, pin12, pin15
  _74161 _74161_2 (
    .pin1(nor_3_out), .pin2(_7474_1_pin3), .pin3(1'b0), .pin4(1'b0), .pin5(1'b0), .pin6(1'b0), .pin7(1'b1),
    .pin8(1'b0), .pin9(1'b1), .pin10(1'b1), .pin11(_74161_2_pin11), .pin12(_74161_2_pin12),
    .pin13(_74161_2_pin13), .pin14(_74161_2_pin14), .pin15(_74161_1_pin7), .pin16(1'b1));
  LED led_1 (.in(_74161_1_pin14));
  and and_1 (IRQ, _7474_2_pin2, _7404_1_pin6);
  LED led_2 (.in(_74161_2_pin12));
  LED led_3 (.in(_74161_2_pin11));
  LED IRQSUP (.in(_7404_1_pin5));
  LED IRQWAIT (.in(_7474_2_pin2));
  LED led_4 (.in(_74161_2_pin14));
  LED led_5 (.in(_74161_2_pin13));
endmodule
