// Digital circuit MemoryManager.dig as structural Verilog
module MemoryManager (
  input  D7,
  input  D6,
  input  D5,
  input  D4,
  input  D3,
  input  D2,
  input  D1,
  input  D0,
  input  EIN_L,
  input  LOAD,
  input  RST,
  input  EIN_H,
  input  EOUT,
  input  EIN,
  input  PG,
  input  P2,
  input  A7,
  input  A6,
  input  A5,
  input  A4,
  input  A3,
  input  A2,
  input  A1,
  input  A0,
  input  INC,
  input  P1,
  input  P0
);

  wire _74161_1_pin11, _74161_1_pin12, _74161_1_pin13, _74161_1_pin14, _74161_2_pin11, _74161_2_pin12,
       _74161_2_pin13, _74161_2_pin14, _74161_3_pin11, _74161_3_pin12, _74161_3_pin13, _74161_3_pin14,
       _74161_4_pin11, _74161_4_pin12, _74161_4_pin13, _74161_4_pin14, and_1_out, and_2_out, and_3_out,
       and_4_out, and_5_out, and_6_out, and_7_out, and_8_out, and_9_out, and_10_out, and_11_out, and_17_out,
       and_18_out, and_19_out, and_20_out, and_21_out, and_22_out, and_23_out, and_24_out, and_25_out,
       and_26_out, and_27_out, driver_1_out, driver_2_out, not_1_out, not_2_out, not_3_out, not_4_out,
       or_12_out;
  wire [7:0] ramdualport_1_d;
  wire [15:0] and_16_out;

  and and_1 (and_1_out, PG, A7);
  and and_2 (and_2_out, PG, A6);
  and and_3 (and_3_out, PG, A5);
  and and_4 (and_4_out, PG, A4);
  and and_5 (and_5_out, PG, A3);
  and and_6 (and_6_out, PG, A2);
  and and_7 (and_7_out, PG, A1);
  and and_8 (and_8_out, PG, A0);
  and and_9 (and_9_out, PG, P2);
  and and_10 (and_10_out, PG, P1);
  and and_11 (and_11_out, PG, P0);
  assign driver_1_out = EIN_H ? LOAD : 1'bz;  // Driver driver_1
  assign driver_2_out = EIN_L ? LOAD : 1'bz;  // Driver driver_2
  PullDown pulldown_1 (.out(driver_1_out));
  PullDown pulldown_2 (.out(driver_2_out));
  not not_1 (not_1_out, EIN_H);
  not not_2 (not_2_out, EIN_L);
  not not_3 (not_3_out, RST);
  _74161 _74161_1 (
    .pin1(not_3_out), .pin2(driver_1_out), .pin3(D4), .pin4(D5), .pin5(D6), .pin6(D7), .pin7(1'b0),
    .pin8(1'b0), .pin9(not_1_out), .pin10(1'b0), .pin11(_74161_1_pin11), .pin12(_74161_1_pin12),
    .pin13(_74161_1_pin13), .pin14(_74161_1_pin14), .pin16(1'b1));  // open: pin15
  _74161 _74161_2 (
    .pin1(not_3_out), .pin2(driver_1_out), .pin3(D0), .pin4(D1), .pin5(D2), .pin6(D3), .pin7(1'b0),
    .pin8(1'b0), .pin9(not_1_out), .pin10(1'b0), .pin11(_74161_2_pin11), .pin12(_74161_2_pin12),
    .pin13(_74161_2_pin13), .pin14(_74161_2_pin14), .pin16(1'b1));  // open: pin15
  _74161 _74161_3 (
    .pin1(not_3_out), .pin2(driver_2_out), .pin3(D4), .pin4(D5), .pin5(D6), .pin6(D7), .pin7(1'b0),
    .pin8(1'b0), .pin9(not_2_out), .pin10(1'b0), .pin11(_74161_3_pin11), .pin12(_74161_3_pin12),
    .pin13(_74161_3_pin13), .pin14(_74161_3_pin14), .pin16(1'b1));  // open: pin15
  _74161 _74161_4 (
    .pin1(not_3_out), .pin2(driver_2_out), .pin3(D0), .pin4(D1), .pin5(D2), .pin6(D3), .pin7(1'b0),
    .pin8(1'b0), .pin9(not_2_out), .pin10(1'b0), .pin11(_74161_4_pin11), .pin12(_74161_4_pin12),
    .pin13(_74161_4_pin13), .pin14(_74161_4_pin14), .pin16(1'b1));  // open: pin15
  not not_4 (not_4_out, PG);
  and and_12 (and_16_out[15], _74161_1_pin11, not_4_out);
  and and_13 (and_16_out[14], _74161_1_pin12, not_4_out);
  and and_14 (and_16_out[13], _74161_1_pin13, not_4_out);
  and and_15 (and_16_out[12], _74161_1_pin14, not_4_out);
  and and_16 (and_16_out[11], _74161_2_pin11, not_4_out);
  and and_17 (and_17_out, _74161_2_pin12, not_4_out);
  and and_18 (and_18_out, _74161_2_pin13, not_4_out);
  and and_19 (and_19_out, _74161_2_pin14, not_4_out);
  and and_20 (and_20_out, _74161_3_pin11, not_4_out);
  and and_21 (and_21_out, _74161_3_pin12, not_4_out);
  and and_22 (and_22_out, _74161_3_pin13, not_4_out);
  and and_23 (and_23_out, _74161_3_pin14, not_4_out);
  and and_24 (and_24_out, _74161_4_pin11, not_4_out);
  and and_25 (and_25_out, _74161_4_pin12, not_4_out);
  and and_26 (and_26_out, _74161_4_pin13, not_4_out);
  and and_27 (and_27_out, _74161_4_pin14, not_4_out);
  or or_1 (and_16_out[10], and_17_out, and_9_out);
  or or_2 (and_16_out[9], and_18_out, and_10_out);
  or or_3 (and_16_out[8], and_19_out, and_11_out);
  or or_4 (and_16_out[7], and_20_out, and_1_out);
  or or_5 (and_16_out[6], and_21_out, and_2_out);
  or or_6 (and_16_out[5], and_22_out, and_3_out);
  or or_7 (and_16_out[4], and_23_out, and_4_out);
  or or_8 (and_16_out[3], and_24_out, and_5_out);
  or or_9 (and_16_out[2], and_25_out, and_6_out);
  or or_10 (and_16_out[1], and_26_out, and_7_out);
  or or_11 (and_16_out[0], and_27_out, and_8_out);
  or or_12 (or_12_out, EIN, PG, EOUT);
  RAMDualPort #(.AddrBits(16), .Bits(8)) ramdualport_1 (
    .A(and_16_out), .Din({D7, D6, D5, D4, D3, D2, D1, D0}), .str(EIN), .C(LOAD), .ld(or_12_out),
    .D(ramdualport_1_d));
  assign D7 = EOUT ? ramdualport_1_d[7] : 1'bz;  // Driver driver_3
  assign D6 = EOUT ? ramdualport_1_d[6] : 1'bz;  // Driver driver_4
  assign D5 = EOUT ? ramdualport_1_d[5] : 1'bz;  // Driver driver_5
  assign D4 = EOUT ? ramdualport_1_d[4] : 1'bz;  // Driver driver_6
  assign D3 = EOUT ? ramdualport_1_d[3] : 1'bz;  // Driver driver_7
  assign D2 = EOUT ? ramdualport_1_d[2] : 1'bz;  // Driver driver_8
  assign D1 = EOUT ? ramdualport_1_d[1] : 1'bz;  // Driver driver_9
  assign D0 = EOUT ? ramdualport_1_d[0] : 1'bz;  // Driver driver_10

  // Notes on the sheet:
  //   D7: pin 5
  //   D6: pin 6
  //   D5: pin 7
  //   D4: pin 8
  //   D3: pin 9
  //   D2: pin 10
  //   D1: pin 11
  //   D0: pin 12
  //   EIN_L: pin 4
  //   LOAD: pin 1
  //   RST: pin 2
  //   EIN_H: pin 3
  //   EOUT: pin 13
  //   EIN: pin 14
  //   PG: pin 16
  //   P2: pin 17
  //   A7: pin 20
  //   A6: pin 21
  //   A5: pin 22
  //   A4: pin 23
  //   A3: pin 24
  //   A2: pin 25
  //   A1: pin 26
  //   A0: pin 27
  //   INC: pin 15
  //   P1: pin 18
  //   P0: pin 19
endmodule
