// Digital circuit PC_TEMP.dig as structural Verilog
module PC_TEMP (
  input  D7,
  input  D6,
  input  D5,
  input  D4,
  input  D3,
  input  D2,
  input  D1,
  input  D0,
  input  L_IN,
  input  RST,
  input  H_IN,
  input  SET,
  input  JMP,
  input  L_OUT,
  input  H_OUT,
  input  OUT,
  output A7,
  output A6,
  output A5,
  output A4,
  output A3,
  output A2,
  output A1,
  output A0,
  output A8,
  output A9,
  output A10,
  output A11,
  output A12,
  output A13,
  output A14,
  output A15
);

  wire _7404_1_pin2, _7404_1_pin4, _7404_2_pin8, _7404_2_pin10, _7404_2_pin12, _7411_1_pin5, _7411_1_pin6,
       _7411_2_pin3, _7411_2_pin6, _7411_2_pin8, _7411_2_pin12, _7432_1_pin3, _74161_1_pin11, _74161_1_pin12,
       _74161_1_pin13, _74161_1_pin14, _74161_2_pin11, _74161_2_pin12, _74161_2_pin13, _74161_2_pin14,
       _74161_3_pin11, _74161_3_pin12, _74161_3_pin13, _74161_3_pin14, _74161_4_pin11, _74161_4_pin12,
       _74161_4_pin13, _74161_4_pin14, _74161_5_pin7, _74161_5_pin11, _74161_5_pin12, _74161_5_pin13,
       _74161_5_pin14, _74161_6_pin7, _74161_6_pin11, _74161_6_pin12, _74161_6_pin13, _74161_6_pin14,
       _74161_7_pin7, _74161_7_pin11, _74161_7_pin12, _74161_7_pin13, _74161_7_pin14, _74161_8_pin11,
       _74161_8_pin12, _74161_8_pin13, _74161_8_pin14;

  _7404 _7404_1 (
    .pin1(H_OUT), .pin2(_7404_1_pin2), .pin3(L_OUT), .pin4(_7404_1_pin4), .pin5(1'b0), .pin7(1'b0),
    .pin9(L_OUT), .pin11(L_OUT), .pin13(L_OUT), .pin14(1'b1));  // open: pin6, pin8, pin10, pin12
  _7411 _7411_1 (
    .pin1(1'b0), .pin2(1'b0), .pin3(H_IN), .pin4(SET), .pin5(_7411_1_pin5), .pin6(_7411_1_pin6), .pin7(1'b0),
    .pin9(1'b0), .pin10(1'b0), .pin11(1'b0), .pin13(1'b0), .pin14(1'b1));  // open: pin8, pin12
  _7411 _7411_2 (
    .pin1(L_IN), .pin2(SET), .pin3(_7411_2_pin3), .pin4(_7411_1_pin5), .pin5(SET), .pin6(_7411_2_pin6),
    .pin7(1'b0), .pin8(_7411_2_pin8), .pin9(SET), .pin10(JMP), .pin11(JMP), .pin12(_7411_2_pin12),
    .pin13(_7411_2_pin3), .pin14(1'b1));
  _7404 _7404_2 (
    .pin1(H_IN), .pin2(_7411_2_pin3), .pin3(L_IN), .pin4(_7411_1_pin5), .pin5(1'b0), .pin7(1'b0),
    .pin8(_7404_2_pin8), .pin9(JMP), .pin10(_7404_2_pin10), .pin11(OUT), .pin12(_7404_2_pin12), .pin13(RST),
    .pin14(1'b1));  // open: pin6
  _7432 _7432_1 (
    .pin1(_7411_2_pin6), .pin2(_7411_2_pin8), .pin3(_7432_1_pin3), .pin4(1'b0), .pin5(1'b0), .pin7(1'b0),
    .pin9(1'b0), .pin10(1'b0), .pin12(1'b0), .pin13(1'b0), .pin14(1'b1));  // open: pin6, pin8, pin11
  _74161 _74161_1 (
    .pin1(1'b1), .pin2(_7411_1_pin6), .pin3(D4), .pin4(D5), .pin5(D6), .pin6(D7), .pin7(1'b1), .pin8(1'b0),
    .pin9(_7411_2_pin3), .pin10(1'b1), .pin11(_74161_1_pin11), .pin12(_74161_1_pin12),
    .pin13(_74161_1_pin13), .pin14(_74161_1_pin14), .pin16(1'b1));  // open: pin15
  _74161 _74161_2 (
    .pin1(1'b1), .pin2(_7411_1_pin6), .pin3(D0), .pin4(D1), .pin5(D2), .pin6(D3), .pin7(1'b1), .pin8(1'b0),
    .pin9(_7411_2_pin3), .pin10(1'b1), .pin11(_74161_2_pin11), .pin12(_74161_2_pin12),
    .pin13(_74161_2_pin13), .pin14(_74161_2_pin14), .pin16(1'b1));  // open: pin15
  _74161 _74161_3 (
    .pin1(1'b1), .pin2(_7411_2_pin12), .pin3(D4), .pin4(D5), .pin5(D6), .pin6(D7), .pin7(1'b1), .pin8(1'b0),
    .pin9(_7411_1_pin5), .pin10(1'b1), .pin11(_74161_3_pin11), .pin12(_74161_3_pin12),
    .pin13(_74161_3_pin13), .pin14(_74161_3_pin14), .pin16(1'b1));  // open: pin15
  _74161 _74161_4 (
    .pin1(1'b1), .pin2(_7411_2_pin12), .pin3(D0), .pin4(D1), .pin5(D2), .pin6(D3), .pin7(1'b1), .pin8(1'b0),
    .pin9(_7411_1_pin5), .pin10(1'b1), .pin11(_74161_4_pin11), .pin12(_74161_4_pin12),
    .pin13(_74161_4_pin13), .pin14(_74161_4_pin14), .pin16(1'b1));  // open: pin15
  _74161 _74161_5 (
    .pin1(_7404_2_pin12), .pin2(_7432_1_pin3), .pin3(_74161_1_pin14), .pin4(_74161_1_pin13),
    .pin5(_74161_1_pin12), .pin6(_74161_1_pin11), .pin7(_74161_5_pin7), .pin8(1'b0), .pin9(_7404_2_pin8),
    .pin10(_74161_5_pin7), .pin11(_74161_5_pin11), .pin12(_74161_5_pin12), .pin13(_74161_5_pin13),
    .pin14(_74161_5_pin14), .pin16(1'b1));  // open: pin15
  _74161 _74161_6 (
    .pin1(_7404_2_pin12), .pin2(_7432_1_pin3), .pin3(_74161_2_pin14), .pin4(_74161_2_pin13),
    .pin5(_74161_2_pin12), .pin6(_74161_2_pin11), .pin7(_74161_6_pin7), .pin8(1'b0), .pin9(_7404_2_pin8),
    .pin10(_74161_6_pin7), .pin11(_74161_6_pin11), .pin12(_74161_6_pin12), .pin13(_74161_6_pin13),
    .pin14(_74161_6_pin14), .pin15(_74161_5_pin7), .pin16(1'b1));
  _74161 _74161_7 (
    .pin1(_7404_2_pin12), .pin2(_7432_1_pin3), .pin3(_74161_3_pin14), .pin4(_74161_3_pin13),
    .pin5(_74161_3_pin12), .pin6(_74161_3_pin11), .pin7(_74161_7_pin7), .pin8(1'b0), .pin9(_7404_2_pin8),
    .pin10(_74161_7_pin7), .pin11(_74161_7_pin11), .pin12(_74161_7_pin12), .pin13(_74161_7_pin13),
    .pin14(_74161_7_pin14), .pin15(_74161_6_pin7), .pin16(1'b1));
  _74161 _74161_8 (
    .pin1(_7404_2_pin12), .pin2(_7432_1_pin3), .pin3(_74161_4_pin14), .pin4(_74161_4_pin13),
    .pin5(_74161_4_pin12), .pin6(_74161_4_pin11), .pin7(1'b1), .pin8(1'b0), .pin9(_7404_2_pin8),
    .pin10(1'b1), .pin11(_74161_8_pin11), .pin12(_74161_8_pin12), .pin13(_74161_8_pin13),
    .pin14(_74161_8_pin14), .pin15(_74161_7_pin7), .pin16(1'b1));
  _74244 _74244_1 (
    .pin1(_7404_2_pin10), .pin2(_74161_6_pin14), .pin3(A15), .pin4(_74161_6_pin13), .pin5(A14),
    .pin6(_74161_6_pin12), .pin7(A13), .pin8(_74161_6_pin11), .pin9(A12), .pin10(1'b0),
    .pin11(_74161_5_pin14), .pin12(A11), .pin13(_74161_5_pin13), .pin14(A10), .pin15(_74161_5_pin12),
    .pin16(A9), .pin17(_74161_5_pin11), .pin18(A8), .pin19(_7404_2_pin10), .pin20(1'b1));
  _74244 _74244_2 (
    .pin1(_7404_2_pin10), .pin2(_74161_8_pin14), .pin3(A7), .pin4(_74161_8_pin13), .pin5(A6),
    .pin6(_74161_8_pin12), .pin7(A5), .pin8(_74161_8_pin11), .pin9(A4), .pin10(1'b0), .pin11(_74161_7_pin14),
    .pin12(A3), .pin13(_74161_7_pin13), .pin14(A2), .pin15(_74161_7_pin12), .pin16(A1),
    .pin17(_74161_7_pin11), .pin18(A0), .pin19(_7404_2_pin10), .pin20(1'b1));
  _74244 _74244_3 (
    .pin1(_7404_1_pin2), .pin2(_74161_6_pin14), .pin3(D7), .pin4(_74161_6_pin13), .pin5(D6),
    .pin6(_74161_6_pin12), .pin7(D5), .pin8(_74161_6_pin11), .pin9(D4), .pin10(1'b0), .pin11(_74161_5_pin14),
    .pin12(D3), .pin13(_74161_5_pin13), .pin14(D2), .pin15(_74161_5_pin12), .pin16(D1),
    .pin17(_74161_5_pin11), .pin18(D0), .pin19(_7404_1_pin2), .pin20(1'b1));
  _74244 _74244_4 (
    .pin1(_7404_1_pin4), .pin2(_74161_8_pin14), .pin3(D7), .pin4(_74161_8_pin13), .pin5(D6),
    .pin6(_74161_8_pin12), .pin7(D5), .pin8(_74161_8_pin11), .pin9(D4), .pin10(1'b0), .pin11(_74161_7_pin14),
    .pin12(D3), .pin13(_74161_7_pin13), .pin14(D2), .pin15(_74161_7_pin12), .pin16(D1),
    .pin17(_74161_7_pin11), .pin18(D0), .pin19(_7404_1_pin4), .pin20(1'b1));

  // Notes on the sheet:
  //   D7: pin 9
  //   D6: pin 10
  //   D5: pin 11
  //   D4: pin 12
  //   D3: pin 13
  //   D2: pin 14
  //   D1: pin 15
  //   D0: pin 16
  //   A7: pin 24
  //   A6: pin 23
  //   A5: pin 22
  //   A4: pin 21
  //   A3: pin 20
  //   A2: pin 19
  //   A1: pin 18
  //   A0: pin 17
  //   A8: pin 25
  //   A9: pin 26
  //   A10: pin 27
  //   A11: pin 28
  //   A12: pin 29
  //   A13: pin 30
  //   A14: pin 31
  //   A15: pin 32
endmodule
