// Digital circuit Programmer.dig as structural Verilog
module Programmer (
);

  wire _28c256_1_p1, _28c256_1_p2, _28c256_1_p3, _28c256_1_p4, _28c256_1_p5, _28c256_1_p6, _28c256_1_p7,
       _28c256_1_p8, _28c256_1_p9, _28c256_1_p10, _28c256_1_p13, _28c256_1_p14, _28c256_1_p15, _28c256_1_p16,
       _28c256_1_p17, _74595_1_pin9, _74595_1_pin11, _74595_1_pin12, _74595_1_pin14;

  // _28c256 _28c256_1: pin names not known; wires that end beside it: _28c256_1_p1, _28c256_1_p2, _28c256_1_p3, _28c256_1_p4, _28c256_1_p5, _28c256_1_p6, _28c256_1_p7, _28c256_1_p8, _28c256_1_p9, _28c256_1_p10, 1'b0, 1'b1, _28c256_1_p13, _28c256_1_p14, _28c256_1_p15, _28c256_1_p16, _28c256_1_p17
  _74595 _74595_1 (
    .pin1(_28c256_1_p9), .pin2(_28c256_1_p8), .pin3(_28c256_1_p7), .pin4(_28c256_1_p6), .pin5(_28c256_1_p5),
    .pin6(_28c256_1_p4), .pin7(_28c256_1_p3), .pin8(1'b0), .pin9(_74595_1_pin9), .pin10(1'b1),
    .pin11(_74595_1_pin11), .pin12(_74595_1_pin12), .pin13(1'b0), .pin14(_74595_1_pin14),
    .pin15(_28c256_1_p10), .pin16(1'b1));
  _74595 _74595_2 (
    .pin1(_28c256_1_p15), .pin2(_28c256_1_p17), .pin3(_28c256_1_p16), .pin4(_28c256_1_p2),
    .pin5(_28c256_1_p13), .pin6(_28c256_1_p1), .pin8(1'b0), .pin10(1'b1), .pin11(_74595_1_pin11),
    .pin12(_74595_1_pin12), .pin13(1'b0), .pin14(_74595_1_pin9), .pin15(_28c256_1_p14), .pin16(1'b1));  // open: pin7, pin9
endmodule
