// Digital circuit RAM-ROM.dig as structural Verilog
module RAM_ROM (
  input  A15,
  input  A14,
  input  A13,
  input  A12,
  input  A11,
  input  M_IN,
  input  M_OUT,
  input  A10,
  input  A9,
  input  A8
);

  wire _7404_1_pin2, _7404_1_pin4, _7404_1_pin6, _7404_1_pin10, _7404_1_pin12, _7408_1_pin3, _7408_1_pin6,
       _7408_1_pin8, _7408_1_pin11, _7408_2_pin3, _7408_2_pin6, _7432_1_pin11, nor_1_out, not_1_out;

  nor nor_1 (nor_1_out, A15, A14, A13, A12, A11, A10, A9, A8);
  not not_1 (not_1_out, nor_1_out);
  _7432 _7432_1 (
    .pin1(1'b0), .pin2(1'b0), .pin4(1'b0), .pin5(1'b0), .pin7(1'b0), .pin9(1'b0), .pin10(1'b0),
    .pin11(_7432_1_pin11), .pin12(M_IN), .pin13(M_OUT), .pin14(1'b1));  // open: pin3, pin6, pin8
  _7408 _7408_1 (
    .pin1(M_OUT), .pin2(not_1_out), .pin3(_7408_1_pin3), .pin4(M_OUT), .pin5(nor_1_out), .pin6(_7408_1_pin6),
    .pin7(1'b0), .pin8(_7408_1_pin8), .pin9(M_OUT), .pin10(_7408_1_pin6), .pin11(_7408_1_pin11),
    .pin12(_7432_1_pin11), .pin13(not_1_out), .pin14(1'b1));
  _7408 _7408_2 (
    .pin1(_7408_1_pin3), .pin2(M_OUT), .pin3(_7408_2_pin3), .pin4(not_1_out), .pin5(M_IN),
    .pin6(_7408_2_pin6), .pin7(1'b0), .pin9(1'b0), .pin10(1'b0), .pin12(1'b0), .pin13(1'b0), .pin14(1'b1));  // open: pin8, pin11
  _7404 _7404_1 (
    .pin1(_7408_1_pin6), .pin2(_7404_1_pin2), .pin3(_7408_1_pin8), .pin4(_7404_1_pin4), .pin5(_7408_1_pin11),
    .pin6(_7404_1_pin6), .pin7(1'b0), .pin9(1'b0), .pin10(_7404_1_pin10), .pin11(_7408_2_pin6),
    .pin12(_7404_1_pin12), .pin13(_7408_2_pin3), .pin14(1'b1));  // open: pin8
  LED HIGH_WE (.in(_7404_1_pin10));
  LED HIGH_OE (.in(_7404_1_pin12));
  LED HIGH_CE (.in(_7404_1_pin6));
  LED LOW_OE (.in(_7404_1_pin4));
  LED LOW_CE (.in(_7404_1_pin2));

  // Notes on the sheet:
  //   Y
  //   X
endmodule
