// Digital circuit REG4.dig as structural Verilog
module REG4 (
  input  D3,
  input  D2,
  input  D1,
  input  D0,
  input  REG_SET,
  input  REG_OUT,
  input  REG_IN,
  input  REG_CLR,
  output M0,
  output M1,
  output M2,
  output M3
);

  wire _7404_1_pin2, _7404_1_pin4, _7404_1_pin6;

  _7404 _7404_1 (
    .pin1(REG_IN), .pin2(_7404_1_pin2), .pin3(REG_CLR), .pin4(_7404_1_pin4), .pin5(REG_OUT),
    .pin6(_7404_1_pin6), .pin7(1'b0), .pin9(1'b0), .pin11(1'b0), .pin13(1'b0), .pin14(1'b1));  // open: pin8, pin10, pin12
  _74161 _74161_1 (
    .pin1(_7404_1_pin4), .pin2(REG_SET), .pin3(D0), .pin4(D1), .pin5(D2), .pin6(D3), .pin7(1'b0),
    .pin8(1'b0), .pin9(_7404_1_pin2), .pin10(1'b0), .pin11(M3), .pin12(M2), .pin13(M1), .pin14(M0),
    .pin16(1'b1));  // open: pin15
  _74244 _74244_1 (
    .pin1(_7404_1_pin6), .pin2(1'b0), .pin3(D0), .pin4(1'b0), .pin5(D1), .pin6(1'b0), .pin7(D2), .pin8(1'b0),
    .pin9(D3), .pin10(1'b0), .pin11(M3), .pin13(M2), .pin15(M1), .pin17(M0), .pin19(_7404_1_pin6),
    .pin20(1'b1));  // open: pin12, pin14, pin16, pin18
endmodule
