// Digital circuit REG8THRU.dig as structural Verilog
module REG8THRU (
  input  D7,
  input  D6,
  input  D5,
  input  D4,
  input  D3,
  input  D2,
  input  D1,
  input  D0,
  input  REG_SET,
  input  REG_OUT,
  input  REG_IN,
  input  R7,
  input  R6,
  input  R5,
  input  R4,
  input  R3,
  input  R2,
  input  R1,
  input  R0,
  output M0,
  output M1,
  output M2,
  output M3,
  output M4,
  output M5,
  output M6,
  output M7
);

  wire _7404_1_pin2, _7404_1_pin4, _7404_1_pin6;

  _7404 _7404_1 (
    .pin1(REG_IN), .pin2(_7404_1_pin2), .pin3(REG_SET), .pin4(_7404_1_pin4), .pin5(REG_OUT),
    .pin6(_7404_1_pin6), .pin7(1'b0), .pin9(1'b0), .pin11(1'b0), .pin13(1'b0), .pin14(1'b1));  // open: pin8, pin10, pin12
  _74161 _74161_1 (
    .pin1(1'b1), .pin2(_7404_1_pin4), .pin3(R4), .pin4(R5), .pin5(R6), .pin6(R7), .pin7(1'b0), .pin8(1'b0),
    .pin9(_7404_1_pin2), .pin10(1'b0), .pin11(M7), .pin12(M6), .pin13(M5), .pin14(M4), .pin16(1'b1));  // open: pin15
  _74161 _74161_2 (
    .pin1(1'b1), .pin2(_7404_1_pin4), .pin3(R0), .pin4(R1), .pin5(R2), .pin6(R3), .pin7(1'b0), .pin8(1'b0),
    .pin9(_7404_1_pin2), .pin10(1'b0), .pin11(M3), .pin12(M2), .pin13(M1), .pin14(M0), .pin16(1'b1));  // open: pin15
  _74244 _74244_1 (
    .pin1(_7404_1_pin6), .pin2(M7), .pin3(D7), .pin4(M6), .pin5(D6), .pin6(M5), .pin7(D5), .pin8(M4),
    .pin9(D4), .pin10(1'b0), .pin11(M3), .pin12(D3), .pin13(M2), .pin14(D2), .pin15(M1), .pin16(D1),
    .pin17(M0), .pin18(D0), .pin19(_7404_1_pin6), .pin20(1'b1));
endmodule
