// Digital circuit Register8_Interrupt.dig as structural Verilog
module Register8_Interrupt (
  input  D7,
  input  D6,
  input  D5,
  input  D4,
  input  D3,
  input  D2,
  input  D1,
  input  D0,
  input  LOAD,
  input  RST,
  input  EOUT,
  input  EIN,
  output M0,
  output M1,
  output M2,
  output M3,
  output M4,
  output M5,
  output M6,
  output M7
);

  wire driver_1_out, not_1_out, not_2_out;

  assign driver_1_out = EIN ? LOAD : 1'bz;  // Driver driver_1
  PullDown pulldown_1 (.out(driver_1_out));
  not not_1 (not_1_out, EIN);
  not not_2 (not_2_out, RST);
  _74161 _74161_1 (
    .pin1(not_2_out), .pin2(driver_1_out), .pin3(D4), .pin4(D5), .pin5(D6), .pin6(D7), .pin7(1'b0),
    .pin8(1'b0), .pin9(not_1_out), .pin10(1'b0), .pin11(M7), .pin12(M6), .pin13(M5), .pin14(M4), .pin16(1'b1));  // open: pin15
  _74161 _74161_2 (
    .pin1(not_2_out), .pin2(driver_1_out), .pin3(D0), .pin4(D1), .pin5(D2), .pin6(D3), .pin7(1'b0),
    .pin8(1'b0), .pin9(not_1_out), .pin10(1'b0), .pin11(M3), .pin12(M2), .pin13(M1), .pin14(M0), .pin16(1'b1));  // open: pin15
  assign D7 = EOUT ? M7 : 1'bz;  // Driver driver_2
  assign D6 = EOUT ? M6 : 1'bz;  // Driver driver_3
  assign D5 = EOUT ? M5 : 1'bz;  // Driver driver_4
  assign D4 = EOUT ? M4 : 1'bz;  // Driver driver_5
  assign D3 = EOUT ? M3 : 1'bz;  // Driver driver_6
  assign D2 = EOUT ? M2 : 1'bz;  // Driver driver_7
  assign D1 = EOUT ? M1 : 1'bz;  // Driver driver_8
  assign D0 = EOUT ? M0 : 1'bz;  // Driver driver_9
endmodule
