// Digital circuit Register_SepOut4.dig as structural Verilog
module Register_SepOut4 (
  input  D3,
  input  D2,
  input  D1,
  input  D0,
  input  LOAD,
  input  RST,
  input  EOUT,
  input  EIN,
  output M0,
  output M1,
  output M2,
  output M3,
  output Q3,
  output Q2,
  output Q1,
  output Q0
);

  wire not_1_out, not_2_out, pulldown_1_out;

  PullDown pulldown_1 (.out(pulldown_1_out));
  assign pulldown_1_out = EIN ? LOAD : 1'bz;  // Driver driver_1
  not not_1 (not_1_out, EIN);
  not not_2 (not_2_out, RST);
  _74161 _74161_1 (
    .pin1(not_2_out), .pin2(pulldown_1_out), .pin3(D0), .pin4(D1), .pin5(D2), .pin6(D3), .pin7(1'b0),
    .pin8(1'b0), .pin9(not_1_out), .pin10(1'b0), .pin11(M3), .pin12(M2), .pin13(M1), .pin14(M0), .pin16(1'b1));  // open: pin15
  assign Q3 = EOUT ? M3 : 1'bz;  // Driver driver_2
  assign Q2 = EOUT ? M2 : 1'bz;  // Driver driver_3
  assign Q1 = EOUT ? M1 : 1'bz;  // Driver driver_4
  assign Q0 = EOUT ? M0 : 1'bz;  // Driver driver_5
endmodule
