// Digital circuit STACK.dig as structural Verilog
module STACK (
  input  POP,
  input  PUSH,
  input  LOAD,
  input  EOUT,
  input  RST,
  output ERR,
  output A7,
  output A6,
  output A5,
  output A4,
  output A3,
  output A2,
  output A1,
  output A0,
  output [7:0] DISPLAY
);

  wire and_1_out, and_2_out, or_1_out, updowncounter_1_err;

  or or_1 (or_1_out, POP, PUSH);
  and and_1 (and_1_out, or_1_out, LOAD);
  UPDOWNCOUNTER updowncounter_1 (
    .UP_DOWN(PUSH), .RST(RST), .LOAD(and_1_out), .Q0(DISPLAY[0]), .Q1(DISPLAY[1]), .Q2(DISPLAY[2]),
    .Q3(DISPLAY[3]), .Q4(DISPLAY[4]), .Q5(DISPLAY[5]), .Q6(DISPLAY[6]), .Q7(DISPLAY[7]),
    .ERR(updowncounter_1_err));
  and and_2 (and_2_out, POP, PUSH);
  or or_2 (ERR, and_2_out, updowncounter_1_err);
  assign A7 = EOUT ? DISPLAY[7] : 1'bz;  // Driver driver_1
  assign A6 = EOUT ? DISPLAY[6] : 1'bz;  // Driver driver_2
  assign A5 = EOUT ? DISPLAY[5] : 1'bz;  // Driver driver_3
  assign A4 = EOUT ? DISPLAY[4] : 1'bz;  // Driver driver_4
  assign A3 = EOUT ? DISPLAY[3] : 1'bz;  // Driver driver_5
  assign A2 = EOUT ? DISPLAY[2] : 1'bz;  // Driver driver_6
  assign A1 = EOUT ? DISPLAY[1] : 1'bz;  // Driver driver_7
  assign A0 = EOUT ? DISPLAY[0] : 1'bz;  // Driver driver_8

  // Notes on the sheet:
  //   Both PUSH and POP
endmodule
