// Digital circuit Test.dig as structural Verilog
module Test (
  input  clk,
  input  EIN,
  input  EOUT,
  input  POP,
  input  PUSH,
  input  ENABLE,
  input  LOAD_CLK,
  input  CLK_2
);

  wire stack_1_p3, stack_1_p4, stack_1_p5, stack_1_p6, stack_1_p7, stack_1_p8, stack_1_p9, stack_1_p10,
       stack_1_p15, stack_1_p16, stack_1_p17, stack_1_p18, stack_1_p19, stack_1_p20, stack_1_p21,
       stack_1_p22, switch_1_b, switch_2_b;

  Switch switch_1 (.A(1'b1), .B(switch_1_b));
  PullDown pulldown_1 (.out(switch_1_b));
  // CLK clk_1: pin names not known; wires that end beside it: clk, switch_1_b
  Switch switch_2 (.A(1'b1), .B(switch_2_b));
  // STACK stack_1: pin names not known; wires that end beside it: POP, PUSH, stack_1_p3, stack_1_p4, stack_1_p5, stack_1_p6, stack_1_p7, stack_1_p8, stack_1_p9, stack_1_p10, LOAD_CLK, EIN, EOUT, switch_2_b, stack_1_p15, stack_1_p16, stack_1_p17, stack_1_p18, stack_1_p19, stack_1_p20, stack_1_p21, stack_1_p22
  PullDown pulldown_2 (.out(switch_2_b));
  LED D7 (.in(stack_1_p15));
  PullDown pulldown_3 (.out(stack_1_p15));
  LED D5 (.in(stack_1_p17));
  LED D6 (.in(stack_1_p16));
  PullDown pulldown_4 (.out(stack_1_p16));
  PullDown pulldown_5 (.out(stack_1_p17));
  LED D3 (.in(stack_1_p19));
  LED D4 (.in(stack_1_p18));
  PullDown pulldown_6 (.out(stack_1_p18));
  PullDown pulldown_7 (.out(stack_1_p19));
  LED D1 (.in(stack_1_p21));
  LED D2 (.in(stack_1_p20));
  PullDown pulldown_8 (.out(stack_1_p20));
  PullDown pulldown_9 (.out(stack_1_p21));
  LED D0 (.in(stack_1_p22));
  LED u_ENABLE (.in(ENABLE));
  PullDown pulldown_10 (.out(stack_1_p22));
  LED LOAD_CHK (.in(LOAD_CLK));
  LED u_CLK_2 (.in(CLK_2));
  LED RST (.in(switch_2_b));
  // PC pc_1: pin names not known; wires that end beside it: stack_1_p15, stack_1_p16, stack_1_p17, stack_1_p18, stack_1_p19, stack_1_p20, stack_1_p21, stack_1_p22, ENABLE, CLK_2, switch_2_b, stack_1_p3, stack_1_p4, stack_1_p5, stack_1_p6, stack_1_p7, stack_1_p8, stack_1_p9, stack_1_p10, stack_1_p3, stack_1_p4, stack_1_p5, stack_1_p6, stack_1_p7, stack_1_p8, stack_1_p9, stack_1_p10
  LED A7 (.in(stack_1_p3));
  LED A6 (.in(stack_1_p4));
  LED A5 (.in(stack_1_p5));
  LED A4 (.in(stack_1_p6));
  LED A3 (.in(stack_1_p7));
  LED A2 (.in(stack_1_p8));
  LED A1 (.in(stack_1_p9));
  LED A0 (.in(stack_1_p10));

  // Notes on the sheet:
  //   CLK - 0
  //   1. CLK
  //   RST - 2
  //   1. NULL
  //   2. CLK
  //   STD - 3
  //   1. ENABLE
  //   2. ENABLE, LOAD-CLK
  //   3. CLK
  //   PUSH - 4
  //   1. ENABLE
  //   2. ENABLE, LOAD-CLK
  //   3. INC
  //   4. PUSH
  //   5. JSRF
  //   6. JSRF, ENABLE
  //   7. JSRF, ENABLE, LOAD-CLK
  //   8. CLK
  //   POP - 5
  //   1. POP
  //   2. ENABLE
  //   3. ENABLE, LOAD-CLK
  //   4. ENABLE,CLK
endmodule
