// Digital circuit Test1.dig as structural Verilog
module Test1 (
  input  UP_DOWN,
  input  RST,
  input  LOAD,
  output QA,
  output QB,
  output QC,
  output QB_2
);

  wire and_1_out, and_2_out, and_3_out, and_4_out, and_5_out, and_6_out, jk_ff_as_1_nq, jk_ff_as_2_nq,
       jk_ff_as_3_nq, not_1_out, or_1_out, or_2_out, or_3_out;

  JK_FF_AS jk_ff_as_1 (.Set(1'b0), .J(1'b1), .C(LOAD), .K(1'b1), .Clr(RST), .Q(QA), .nQ(jk_ff_as_1_nq));
  not not_1 (not_1_out, UP_DOWN);
  and and_1 (and_1_out, UP_DOWN, QA);
  and and_2 (and_2_out, jk_ff_as_1_nq, not_1_out);
  or or_1 (or_1_out, and_1_out, and_2_out);
  JK_FF_AS jk_ff_as_2 (.Set(1'b0), .J(or_1_out), .C(LOAD), .K(or_1_out), .Clr(RST), .Q(QB), .nQ(jk_ff_as_2_nq));
  and and_3 (and_3_out, and_1_out, QB);
  and and_4 (and_4_out, jk_ff_as_2_nq, and_2_out);
  or or_2 (or_2_out, and_3_out, and_4_out);
  JK_FF_AS jk_ff_as_3 (.Set(1'b0), .J(or_2_out), .C(LOAD), .K(or_2_out), .Clr(RST), .Q(QC), .nQ(jk_ff_as_3_nq));
  and and_5 (and_5_out, and_3_out, QC);
  and and_6 (and_6_out, jk_ff_as_3_nq, and_4_out);
  or or_3 (or_3_out, and_5_out, and_6_out);
  JK_FF_AS jk_ff_as_4 (.Set(1'b0), .J(or_3_out), .C(LOAD), .K(or_3_out), .Clr(RST), .Q(QB_2));  // open: nQ
endmodule
