// Digital circuit Test2.dig as structural Verilog
module Test2 (
  input  clk,
  input  in_4,
  output out_2,
  output out_3
);

  wire nand_1_out, nand_2_out, nand_3_out, nand_4_out;

  nand nand_1 (nand_1_out, nand_4_out, nand_2_out);
  nand nand_2 (nand_2_out, nand_1_out, clk);
  nand nand_3 (nand_3_out, nand_2_out, clk, nand_4_out);
  nand nand_4 (nand_4_out, nand_3_out, in_4);
  nand nand_5 (out_2, nand_2_out, out_3);
  nand nand_6 (out_3, out_2, nand_3_out);
endmodule
