// Digital circuit Test3.dig as structural Verilog
module Test3 (
  input  clk
);

  wire and_1_out, d_ff_1_q, d_ff_2_nq, d_ff_2_q, d_ff_3_q, rs_ff_as_1_nq, rs_ff_as_1_q, switch_1_b,
       switch_2_b;

  Switch switch_1 (.A(1'b1), .B(switch_1_b));
  Switch switch_2 (.A(1'b1), .B(switch_2_b));
  PullDown pulldown_1 (.out(switch_1_b));
  PullDown pulldown_2 (.out(switch_2_b));
  D_FF d_ff_1 (.D(switch_1_b), .C(clk), .Q(d_ff_1_q));  // open: nQ
  D_FF d_ff_2 (.D(d_ff_1_q), .C(clk), .Q(d_ff_2_q), .nQ(d_ff_2_nq));
  D_FF d_ff_3 (.D(d_ff_2_nq), .C(clk), .Q(d_ff_3_q));  // open: nQ
  and and_1 (and_1_out, d_ff_2_q, d_ff_3_q);
  LED led_1 (.in(and_1_out));
  RS_FF_AS rs_ff_as_1 (.S(and_1_out), .R(switch_2_b), .Q(rs_ff_as_1_q), .nQ(rs_ff_as_1_nq));
  LED led_2 (.in(rs_ff_as_1_q));
  LED led_3 (.in(rs_ff_as_1_nq));
endmodule
