// Digital circuit Test_PC.dig as structural Verilog
module Test_PC (
  input  L_IN,
  input  RST,
  input  H_IN,
  input  SET,
  input  JMP,
  input  L_OUT,
  input  H_OUT,
  input  OUT
);

  wire _7404_1_pin2, _7404_1_pin4, _7404_2_pin8, _7404_2_pin10, _7404_2_pin12, _7411_1_pin5, _7411_1_pin6,
       _7411_2_pin3, _7411_2_pin6, _7411_2_pin8, _7411_2_pin12, _7432_1_pin3, not_1_out, not_2_out,
       not_3_out, not_4_out, not_5_out, not_6_out, not_7_out;

  _7404 _7404_1 (
    .pin1(H_OUT), .pin2(_7404_1_pin2), .pin3(L_OUT), .pin4(_7404_1_pin4), .pin5(1'b0), .pin7(1'b0),
    .pin9(L_OUT), .pin11(L_OUT), .pin13(L_OUT), .pin14(1'b1));  // open: pin6, pin8, pin10, pin12
  _7411 _7411_1 (
    .pin1(1'b0), .pin2(1'b0), .pin3(H_IN), .pin4(SET), .pin5(_7411_1_pin5), .pin6(_7411_1_pin6), .pin7(1'b0),
    .pin9(1'b0), .pin10(1'b0), .pin11(1'b0), .pin13(1'b0), .pin14(1'b1));  // open: pin8, pin12
  _7411 _7411_2 (
    .pin1(L_IN), .pin2(SET), .pin3(_7411_2_pin3), .pin4(_7411_1_pin5), .pin5(SET), .pin6(_7411_2_pin6),
    .pin7(1'b0), .pin8(_7411_2_pin8), .pin9(SET), .pin10(JMP), .pin11(JMP), .pin12(_7411_2_pin12),
    .pin13(_7411_2_pin3), .pin14(1'b1));
  _7404 _7404_2 (
    .pin1(H_IN), .pin2(_7411_2_pin3), .pin3(L_IN), .pin4(_7411_1_pin5), .pin5(1'b0), .pin7(1'b0),
    .pin8(_7404_2_pin8), .pin9(JMP), .pin10(_7404_2_pin10), .pin11(OUT), .pin12(_7404_2_pin12), .pin13(RST),
    .pin14(1'b1));  // open: pin6
  not not_1 (not_1_out, _7404_1_pin2);
  not not_2 (not_2_out, _7404_1_pin4);
  not not_3 (not_3_out, _7404_2_pin10);
  not not_4 (not_4_out, _7404_2_pin12);
  not not_5 (not_5_out, _7411_2_pin3);
  not not_6 (not_6_out, _7411_1_pin5);
  not not_7 (not_7_out, _7404_2_pin8);
  _7432 _7432_1 (
    .pin1(_7411_2_pin6), .pin2(_7411_2_pin8), .pin3(_7432_1_pin3), .pin4(1'b0), .pin5(1'b0), .pin7(1'b0),
    .pin9(1'b0), .pin10(1'b0), .pin12(1'b0), .pin13(1'b0), .pin14(1'b1));  // open: pin6, pin8, pin11
  LED u_H_OUT (.in(not_1_out));
  LED u_L_OUT (.in(not_2_out));
  LED u_OUT (.in(not_3_out));
  LED CLR (.in(not_4_out));
  LED LOAD_H (.in(not_5_out));
  LED CLK_H (.in(_7411_1_pin6));
  LED LOAD_L (.in(not_6_out));
  LED CHK_L (.in(_7411_2_pin12));
  LED LOAD_PC (.in(not_7_out));
  LED CHK_PC (.in(_7432_1_pin3));
endmodule
