// Digital circuit UPDOWNCOUNTER.dig as structural Verilog
module UPDOWNCOUNTER (
  input  UP_DOWN,
  input  RST,
  input  LOAD,
  output Q0,
  output Q1,
  output Q2,
  output Q3,
  output Q4,
  output Q5,
  output Q6,
  output Q7,
  output ERR
);

  wire and_1_out, and_2_out, and_3_out, and_4_out, and_5_out, and_6_out, and_7_out, and_8_out, and_9_out,
       and_10_out, and_11_out, and_12_out, and_13_out, and_14_out, and_15_out, and_16_out, jk_ff_as_1_nq,
       jk_ff_as_2_nq, jk_ff_as_3_nq, jk_ff_as_4_nq, jk_ff_as_5_nq, jk_ff_as_6_nq, jk_ff_as_7_nq,
       jk_ff_as_8_nq, not_1_out, or_1_out, or_2_out, or_3_out, or_4_out, or_5_out, or_6_out, or_7_out,
       or_8_out;

  JK_FF_AS jk_ff_as_1 (.Set(1'b0), .J(1'b1), .C(LOAD), .K(1'b1), .Clr(RST), .Q(Q0), .nQ(jk_ff_as_1_nq));
  not not_1 (not_1_out, UP_DOWN);
  and and_1 (and_1_out, UP_DOWN, Q0);
  and and_2 (and_2_out, jk_ff_as_1_nq, not_1_out);
  or or_1 (or_1_out, and_1_out, and_2_out);
  JK_FF_AS jk_ff_as_2 (.Set(1'b0), .J(or_1_out), .C(LOAD), .K(or_1_out), .Clr(RST), .Q(Q1), .nQ(jk_ff_as_2_nq));
  and and_3 (and_3_out, and_1_out, Q1);
  and and_4 (and_4_out, jk_ff_as_2_nq, and_2_out);
  or or_2 (or_2_out, and_3_out, and_4_out);
  JK_FF_AS jk_ff_as_3 (.Set(1'b0), .J(or_2_out), .C(LOAD), .K(or_2_out), .Clr(RST), .Q(Q2), .nQ(jk_ff_as_3_nq));
  and and_5 (and_5_out, and_3_out, Q2);
  and and_6 (and_6_out, jk_ff_as_3_nq, and_4_out);
  or or_3 (or_3_out, and_5_out, and_6_out);
  JK_FF_AS jk_ff_as_4 (.Set(1'b0), .J(or_3_out), .C(LOAD), .K(or_3_out), .Clr(RST), .Q(Q3), .nQ(jk_ff_as_4_nq));
  and and_7 (and_7_out, and_5_out, Q3);
  and and_8 (and_8_out, jk_ff_as_4_nq, and_6_out);
  or or_4 (or_4_out, and_7_out, and_8_out);
  JK_FF_AS jk_ff_as_5 (.Set(1'b0), .J(or_4_out), .C(LOAD), .K(or_4_out), .Clr(RST), .Q(Q4), .nQ(jk_ff_as_5_nq));
  and and_9 (and_9_out, and_7_out, Q4);
  and and_10 (and_10_out, jk_ff_as_5_nq, and_8_out);
  or or_5 (or_5_out, and_9_out, and_10_out);
  JK_FF_AS jk_ff_as_6 (.Set(1'b0), .J(or_5_out), .C(LOAD), .K(or_5_out), .Clr(RST), .Q(Q5), .nQ(jk_ff_as_6_nq));
  and and_11 (and_11_out, and_9_out, Q5);
  and and_12 (and_12_out, jk_ff_as_6_nq, and_10_out);
  or or_6 (or_6_out, and_11_out, and_12_out);
  JK_FF_AS jk_ff_as_7 (.Set(1'b0), .J(or_6_out), .C(LOAD), .K(or_6_out), .Clr(RST), .Q(Q6), .nQ(jk_ff_as_7_nq));
  and and_13 (and_13_out, and_11_out, Q6);
  and and_14 (and_14_out, jk_ff_as_7_nq, and_12_out);
  or or_7 (or_7_out, and_13_out, and_14_out);
  JK_FF_AS jk_ff_as_8 (.Set(1'b0), .J(or_7_out), .C(LOAD), .K(or_7_out), .Clr(RST), .Q(Q7), .nQ(jk_ff_as_8_nq));
  and and_15 (and_15_out, and_13_out, Q7);
  and and_16 (and_16_out, jk_ff_as_8_nq, and_14_out);
  or or_8 (or_8_out, and_15_out, and_16_out);
  JK_FF_AS jk_ff_as_9 (.Set(1'b0), .J(or_8_out), .C(LOAD), .K(or_8_out), .Clr(RST), .Q(ERR));  // open: nQ

  // Notes on the sheet:
  //   UP_DOWN: pin 2
  //   Q0: pin 12
  //   Q1: pin 11
  //   Q2: pin 10
  //   RST: pin 1
  //   LOAD: pin 3
  //   Q3: pin 9
  //   Q4: pin 8
  //   Q5: pin 7
  //   Q6: pin 6
  //   Q7: pin 5
  //   ERR: pin 4
endmodule
