// Digital circuit WMEM.dig as structural Verilog
module WMEM (
  input  A0,
  input  A1,
  input  A2,
  input  A3,
  input  A4,
  input  A5,
  input  A6,
  input  A7,
  input  EOUT,
  input  EIN,
  input  D0,
  input  D1,
  input  D2,
  input  D3,
  input  D4,
  input  D5,
  input  D6,
  input  D7,
  input  CLK,
  output Q0,
  output Q1,
  output Q2,
  output Q3,
  output Q4,
  output Q5,
  output Q6,
  output Q7
);

  wire or_1_out;
  wire [7:0] ramdualport_1_d;

  RAMDualPort #(.AddrBits(8), .Bits(8)) ramdualport_1 (
    .A({A7, A6, A5, A4, A3, A2, A1, A0}), .Din({D7, D6, D5, D4, D3, D2, D1, D0}), .str(EIN), .C(CLK),
    .ld(or_1_out), .D(ramdualport_1_d));
  or or_1 (or_1_out, EOUT, EIN);
  assign Q0 = EOUT ? ramdualport_1_d[0] : 1'bz;  // Driver driver_1
  assign Q1 = EOUT ? ramdualport_1_d[1] : 1'bz;  // Driver driver_2
  assign Q2 = EOUT ? ramdualport_1_d[2] : 1'bz;  // Driver driver_3
  assign Q3 = EOUT ? ramdualport_1_d[3] : 1'bz;  // Driver driver_4
  assign Q4 = EOUT ? ramdualport_1_d[4] : 1'bz;  // Driver driver_5
  assign Q5 = EOUT ? ramdualport_1_d[5] : 1'bz;  // Driver driver_6
  assign Q6 = EOUT ? ramdualport_1_d[6] : 1'bz;  // Driver driver_7
  assign Q7 = EOUT ? ramdualport_1_d[7] : 1'bz;  // Driver driver_8
endmodule
